// Logisim project Calculator.circ as structural Verilog: 17 circuits, main circuit CALCULATOR
module main (
  input  [4:0] in_1,
  input  [3:0] in_2
);

  wire b8tctobcd_1_p0, b8tctobcd_1_p1, b8tctobcd_1_p2, b8tctobcd_1_p3, b8tctobcd_1_p4, b8tctobcd_1_p5,
       b8tctobcd_1_p6, b8tctobcd_1_p7, b8tctobcd_1_p8, b8tctobcd_1_p9, n7447_1_pin2, n7447_1_pin3,
       n7447_1_pin9, n7447_1_pin10, n7447_1_pin11, n7447_1_pin12, n7447_1_pin13, n7447_1_pin14,
       n7447_1_pin15, n7447_2_pin9, n7447_2_pin10, n7447_2_pin11, n7447_2_pin12, n7447_2_pin13,
       n7447_2_pin14, n7447_2_pin15, n7447_3_pin9, n7447_3_pin10, n7447_3_pin11, n7447_3_pin12,
       n7447_3_pin13, n7447_3_pin14, n7447_3_pin15, not_1_out, not_2_out, not_3_out, not_4_out, not_5_out,
       not_6_out, not_7_out, not_8_out, not_9_out, not_10_out, not_11_out, not_12_out, not_13_out,
       not_14_out, not_15_out, not_16_out, not_17_out, not_18_out, not_19_out, not_20_out, not_21_out;
  wire [7:0] multiplie_1_out_3;

  Multiplie multiplie_1 (.in_1(in_1), .in_2(in_2), .out_3(multiplie_1_out_3));
  B8TCTOBCD b8tctobcd_1 (
    .B0(multiplie_1_out_3[0]), .B1(multiplie_1_out_3[1]), .B2(multiplie_1_out_3[2]),
    .B3(multiplie_1_out_3[3]), .B4(multiplie_1_out_3[4]), .B5(multiplie_1_out_3[5]),
    .B6(multiplie_1_out_3[6]), .B7(multiplie_1_out_3[7]), .P0(b8tctobcd_1_p0), .P1(b8tctobcd_1_p1),
    .P2(b8tctobcd_1_p2), .P3(b8tctobcd_1_p3), .P4(b8tctobcd_1_p4), .P5(b8tctobcd_1_p5), .P6(b8tctobcd_1_p6),
    .P7(b8tctobcd_1_p7), .P8(b8tctobcd_1_p8), .P9(b8tctobcd_1_p9));  // open: B8, B9, P10, P11
  not not_1 (not_1_out, n7447_1_pin9);
  not not_2 (not_2_out, n7447_1_pin10);
  not not_3 (not_3_out, n7447_1_pin11);
  not not_4 (not_4_out, n7447_1_pin12);
  _7_Segment_Display u_7_segment_display_1 (
    .g(not_6_out), .f(not_7_out), .a(not_5_out), .b(not_4_out), .e(not_1_out), .d(not_2_out), .c(not_3_out));  // open: dp
  not not_5 (not_5_out, n7447_1_pin13);
  not not_6 (not_6_out, n7447_1_pin14);
  not not_7 (not_7_out, n7447_1_pin15);
  not not_8 (not_8_out, n7447_2_pin9);
  not not_9 (not_9_out, n7447_2_pin10);
  _7447 u_7447_1 (
    .pin1(b8tctobcd_1_p9), .pin2(n7447_1_pin2), .pin3(n7447_1_pin3), .pin4(n7447_1_pin3),
    .pin5(n7447_1_pin3), .pin6(n7447_1_pin2), .pin7(b8tctobcd_1_p8), .pin15(n7447_1_pin15),
    .pin14(n7447_1_pin14), .pin13(n7447_1_pin13), .pin12(n7447_1_pin12), .pin11(n7447_1_pin11),
    .pin10(n7447_1_pin10), .pin9(n7447_1_pin9));
  not not_10 (not_10_out, n7447_2_pin11);
  not not_11 (not_11_out, n7447_2_pin12);
  not not_12 (not_12_out, n7447_2_pin13);
  not not_13 (not_13_out, n7447_2_pin14);
  _7_Segment_Display u_7_segment_display_2 (
    .g(not_13_out), .f(not_14_out), .a(not_12_out), .b(not_11_out), .e(not_8_out), .d(not_9_out),
    .c(not_10_out));  // open: dp
  _7447 u_7447_2 (
    .pin1(b8tctobcd_1_p5), .pin2(b8tctobcd_1_p6), .pin3(n7447_1_pin3), .pin4(n7447_1_pin3),
    .pin5(n7447_1_pin3), .pin6(b8tctobcd_1_p7), .pin7(b8tctobcd_1_p4), .pin15(n7447_2_pin15),
    .pin14(n7447_2_pin14), .pin13(n7447_2_pin13), .pin12(n7447_2_pin12), .pin11(n7447_2_pin11),
    .pin10(n7447_2_pin10), .pin9(n7447_2_pin9));
  not not_14 (not_14_out, n7447_2_pin15);
  not not_15 (not_15_out, n7447_3_pin9);
  not not_16 (not_16_out, n7447_3_pin10);
  not not_17 (not_17_out, n7447_3_pin11);
  not not_18 (not_18_out, n7447_3_pin12);
  _7_Segment_Display u_7_segment_display_3 (
    .g(not_20_out), .f(not_21_out), .a(not_19_out), .b(not_18_out), .e(not_15_out), .d(not_16_out),
    .c(not_17_out));  // open: dp
  not not_19 (not_19_out, n7447_3_pin13);
  not not_20 (not_20_out, n7447_3_pin14);
  not not_21 (not_21_out, n7447_3_pin15);
  _7447 u_7447_3 (
    .pin1(b8tctobcd_1_p1), .pin2(b8tctobcd_1_p2), .pin3(n7447_1_pin3), .pin4(n7447_1_pin3),
    .pin5(n7447_1_pin3), .pin6(b8tctobcd_1_p3), .pin7(b8tctobcd_1_p0), .pin15(n7447_3_pin15),
    .pin14(n7447_3_pin14), .pin13(n7447_3_pin13), .pin12(n7447_3_pin12), .pin11(n7447_3_pin11),
    .pin10(n7447_3_pin10), .pin9(n7447_3_pin9));
  // also tied to GND on the sheet: n7447_1_pin2
  // also tied to VCC on the sheet: n7447_1_pin3
endmodule

module ADD3 (
  input  A0,
  input  A1,
  input  A2,
  input  A3,
  output S0,
  output S1,
  output S2,
  output S3
);

  wire and_1_out, and_2_out, and_3_out, and_4_out, and_5_out, and_6_out, and_7_out, and_8_out, and_9_out,
       and_10_out, not_1_out, not_2_out, not_3_out, not_4_out;

  not not_1 (not_1_out, A0);
  not not_2 (not_2_out, A1);
  not not_3 (not_3_out, A2);
  not not_4 (not_4_out, A3);
  and and_1 (and_1_out, A2, A0);
  and and_2 (and_2_out, A2, A1);
  and and_3 (and_3_out, A2, not_2_out, not_1_out);
  and and_4 (and_4_out, A3, A0);
  and and_5 (and_5_out, not_3_out, A1);
  and and_6 (and_6_out, A1, A0);
  and and_7 (and_7_out, A3, not_1_out);
  and and_8 (and_8_out, not_4_out, not_3_out, A0);
  and and_9 (and_9_out, A3, not_1_out);
  and and_10 (and_10_out, A2, A1, not_1_out);
  or or_1 (S0, and_8_out, and_9_out, and_10_out);
  or or_2 (S1, and_5_out, and_6_out, and_7_out);
  or or_3 (S2, and_3_out, and_4_out);
  or or_4 (S3, and_1_out, A3, and_2_out);

  // Notes on the sheet:
  //   ADD
  //   If the amount is greater than or equal to 5
  //   3
endmodule

module B8TOBCD (
  input  B0,
  input  B1,
  input  B2,
  input  B3,
  input  B4,
  input  B5,
  input  B6,
  input  B7,
  input  B8,
  input  B9,
  output P0,
  output P1,
  output P2,
  output P3,
  output P4,
  output P5,
  output P6,
  output P7,
  output P8,
  output P9,
  output P10,
  output P11,
  output out_23,
  output out_24,
  output P11_2,
  output out_26,
  output out_27,
  output P11_3,
  output out_29,
  output out_30,
  output P11_4
);

  wire add3_1_s0, add3_1_s1, add3_1_s2, add3_1_s3, add3_2_s0, add3_2_s1, add3_2_s2, add3_2_s3, add3_3_s0,
       add3_3_s1, add3_3_s2, add3_3_s3, add3_4_s0, add3_4_s1, add3_4_s2, add3_4_s3, add3_5_s0, add3_5_s1,
       add3_5_s2, add3_5_s3, add3_6_s0, add3_6_s1, add3_6_s2, add3_6_s3, add3_7_s0, add3_7_s1, add3_7_s2,
       add3_7_s3, add3_8_s0, add3_8_s1, add3_8_s2, add3_8_s3, add3_9_s0, add3_9_s1, add3_9_s2, add3_9_s3,
       add3_10_s0, add3_10_s1, add3_10_s2, add3_10_s3, add3_11_s0, add3_11_s1, add3_11_s2, add3_11_s3,
       add3_12_s0, add3_12_s1, add3_12_s2, add3_12_s3, add3_13_s0, add3_13_s1, add3_13_s2, add3_13_s3,
       add3_14_s0, add3_14_s1, add3_14_s2, add3_14_s3, add3_15_s0, add3_15_s1, add3_15_s2, add3_15_s3,
       add3_16_s0, add3_16_s1, add3_16_s2, add3_16_s3, add3_17_s0, add3_17_s1, add3_17_s2, add3_17_s3,
       add3_18_s0, add3_18_s1, add3_18_s2, add3_18_s3, add3_19_s0, add3_19_s1, add3_19_s2, add3_19_s3,
       add3_20_s0, add3_20_s1, add3_20_s2, add3_20_s3, add3_21_s0, add3_21_s1, add3_21_s2, add3_21_s3,
       add3_22_s0, add3_22_s1, add3_22_s2, add3_22_s3, add3_23_s0, add3_23_s1, add3_23_s2, add3_23_s3,
       add3_24_s0, add3_24_s1, add3_24_s2, add3_24_s3, add3_25_s0, add3_25_s1, add3_25_s2, add3_25_s3,
       add3_26_s0, add3_26_s1, add3_26_s2, add3_26_s3, add3_27_s0, add3_27_s1, add3_27_s2, add3_27_s3,
       add3_28_s0, add3_28_s1, add3_28_s2, add3_28_s3, add3_29_s0, add3_29_s1, add3_29_s2, add3_29_s3,
       add3_30_s0, add3_30_s1, add3_30_s2, add3_30_s3;

  ADD3 add3_1 (
    .A1(1'b0), .A2(1'b0), .A3(1'b0), .A0(1'b0), .S0(add3_1_s0), .S1(add3_1_s1), .S2(add3_1_s2), .S3(add3_1_s3));
  ADD3 add3_2 (
    .A1(add3_1_s0), .A2(add3_1_s1), .A3(add3_1_s2), .A0(1'b0), .S0(add3_2_s0), .S1(add3_2_s1),
    .S2(add3_2_s2), .S3(add3_2_s3));
  ADD3 add3_3 (
    .A1(add3_2_s0), .A2(add3_2_s1), .A3(add3_2_s2), .A0(1'b0), .S0(add3_3_s0), .S1(add3_3_s1),
    .S2(add3_3_s2), .S3(add3_3_s3));
  ADD3 add3_4 (
    .A1(add3_3_s0), .A2(add3_3_s1), .A3(add3_3_s2), .A0(1'b0), .S0(add3_4_s0), .S1(add3_4_s1),
    .S2(add3_4_s2), .S3(add3_4_s3));
  ADD3 add3_5 (
    .A1(add3_2_s3), .A2(add3_1_s3), .A3(1'b0), .A0(add3_3_s3), .S0(add3_5_s0), .S1(add3_5_s1),
    .S2(add3_5_s2), .S3(add3_5_s3));
  ADD3 add3_6 (
    .A1(add3_4_s0), .A2(add3_4_s1), .A3(add3_4_s2), .A0(B9), .S0(add3_6_s0), .S1(add3_6_s1), .S2(add3_6_s2),
    .S3(add3_6_s3));
  ADD3 add3_7 (
    .A1(add3_5_s0), .A2(add3_5_s1), .A3(add3_5_s2), .A0(add3_4_s3), .S0(add3_7_s0), .S1(add3_7_s1),
    .S2(add3_7_s2), .S3(add3_7_s3));
  ADD3 add3_8 (
    .A1(add3_6_s0), .A2(add3_6_s1), .A3(add3_6_s2), .A0(B8), .S0(add3_8_s0), .S1(add3_8_s1), .S2(add3_8_s2),
    .S3(add3_8_s3));
  ADD3 add3_9 (
    .A1(add3_7_s0), .A2(add3_7_s1), .A3(add3_7_s2), .A0(add3_6_s3), .S0(add3_9_s0), .S1(add3_9_s1),
    .S2(add3_9_s2), .S3(add3_9_s3));
  ADD3 add3_10 (
    .A1(add3_8_s0), .A2(add3_8_s1), .A3(add3_8_s2), .A0(B7), .S0(add3_10_s0), .S1(add3_10_s1),
    .S2(add3_10_s2), .S3(add3_10_s3));
  ADD3 add3_11 (
    .A1(add3_9_s0), .A2(add3_9_s1), .A3(add3_9_s2), .A0(add3_8_s3), .S0(add3_11_s0), .S1(add3_11_s1),
    .S2(add3_11_s2), .S3(add3_11_s3));
  ADD3 add3_12 (
    .A1(add3_7_s3), .A2(add3_5_s3), .A3(1'b0), .A0(add3_9_s3), .S0(add3_12_s0), .S1(add3_12_s1),
    .S2(add3_12_s2), .S3(add3_12_s3));
  ADD3 add3_13 (
    .A1(add3_10_s0), .A2(add3_10_s1), .A3(add3_10_s2), .A0(B6), .S0(add3_13_s0), .S1(add3_13_s1),
    .S2(add3_13_s2), .S3(add3_13_s3));
  ADD3 add3_14 (
    .A1(add3_11_s0), .A2(add3_11_s1), .A3(add3_11_s2), .A0(add3_10_s3), .S0(add3_14_s0), .S1(add3_14_s1),
    .S2(add3_14_s2), .S3(add3_14_s3));
  ADD3 add3_15 (
    .A1(add3_12_s0), .A2(add3_12_s1), .A3(add3_12_s2), .A0(add3_11_s3), .S0(add3_15_s0), .S1(add3_15_s1),
    .S2(add3_15_s2), .S3(add3_15_s3));
  ADD3 add3_16 (
    .A1(add3_13_s0), .A2(add3_13_s1), .A3(add3_13_s2), .A0(B5), .S0(add3_16_s0), .S1(add3_16_s1),
    .S2(add3_16_s2), .S3(add3_16_s3));
  ADD3 add3_17 (
    .A1(add3_14_s0), .A2(add3_14_s1), .A3(add3_14_s2), .A0(add3_13_s3), .S0(add3_17_s0), .S1(add3_17_s1),
    .S2(add3_17_s2), .S3(add3_17_s3));
  ADD3 add3_18 (
    .A1(add3_15_s0), .A2(add3_15_s1), .A3(add3_15_s2), .A0(add3_14_s3), .S0(add3_18_s0), .S1(add3_18_s1),
    .S2(add3_18_s2), .S3(add3_18_s3));
  ADD3 add3_19 (
    .A1(add3_16_s0), .A2(add3_16_s1), .A3(add3_16_s2), .A0(B4), .S0(add3_19_s0), .S1(add3_19_s1),
    .S2(add3_19_s2), .S3(add3_19_s3));
  ADD3 add3_20 (
    .A1(add3_17_s0), .A2(add3_17_s1), .A3(add3_17_s2), .A0(add3_16_s3), .S0(add3_20_s0), .S1(add3_20_s1),
    .S2(add3_20_s2), .S3(add3_20_s3));
  ADD3 add3_21 (
    .A1(add3_18_s0), .A2(add3_18_s1), .A3(add3_18_s2), .A0(add3_17_s3), .S0(add3_21_s0), .S1(add3_21_s1),
    .S2(add3_21_s2), .S3(add3_21_s3));
  ADD3 add3_22 (
    .A1(add3_15_s3), .A2(add3_12_s3), .A3(1'b0), .A0(add3_18_s3), .S0(add3_22_s0), .S1(add3_22_s1),
    .S2(add3_22_s2), .S3(add3_22_s3));
  ADD3 add3_23 (
    .A1(add3_19_s0), .A2(add3_19_s1), .A3(add3_19_s2), .A0(B3), .S0(add3_23_s0), .S1(add3_23_s1),
    .S2(add3_23_s2), .S3(add3_23_s3));
  ADD3 add3_24 (
    .A1(add3_20_s0), .A2(add3_20_s1), .A3(add3_20_s2), .A0(add3_19_s3), .S0(add3_24_s0), .S1(add3_24_s1),
    .S2(add3_24_s2), .S3(add3_24_s3));
  ADD3 add3_25 (
    .A1(add3_21_s0), .A2(add3_21_s1), .A3(add3_21_s2), .A0(add3_20_s3), .S0(add3_25_s0), .S1(add3_25_s1),
    .S2(add3_25_s2), .S3(add3_25_s3));
  ADD3 add3_26 (
    .A1(add3_22_s0), .A2(add3_22_s1), .A3(add3_22_s2), .A0(add3_21_s3), .S0(add3_26_s0), .S1(add3_26_s1),
    .S2(add3_26_s2), .S3(add3_26_s3));
  ADD3 add3_27 (
    .A1(add3_23_s0), .A2(add3_23_s1), .A3(add3_23_s2), .A0(B2), .S0(add3_27_s0), .S1(add3_27_s1),
    .S2(add3_27_s2), .S3(add3_27_s3));
  ADD3 add3_28 (
    .A1(add3_24_s0), .A2(add3_24_s1), .A3(add3_24_s2), .A0(add3_23_s3), .S0(add3_28_s0), .S1(add3_28_s1),
    .S2(add3_28_s2), .S3(add3_28_s3));
  ADD3 add3_29 (
    .A1(add3_25_s0), .A2(add3_25_s1), .A3(add3_25_s2), .A0(add3_24_s3), .S0(add3_29_s0), .S1(add3_29_s1),
    .S2(add3_29_s2), .S3(add3_29_s3));
  ADD3 add3_30 (
    .A1(add3_26_s0), .A2(add3_26_s1), .A3(add3_26_s2), .A0(add3_25_s3), .S0(add3_30_s0), .S1(add3_30_s1),
    .S2(add3_30_s2), .S3(add3_30_s3));
  ADD3 add3_31 (.A1(add3_27_s0), .A2(add3_27_s1), .A3(add3_27_s2), .A0(B1), .S0(P1), .S1(P2), .S2(P3), .S3(P4));
  ADD3 add3_32 (.A1(add3_28_s0), .A2(add3_28_s1), .A3(add3_28_s2), .A0(add3_27_s3), .S0(P5), .S1(P6), .S2(P7), .S3(P8));
  ADD3 add3_33 (
    .A1(add3_29_s0), .A2(add3_29_s1), .A3(add3_29_s2), .A0(add3_28_s3), .S0(P9), .S1(P10), .S2(P11),
    .S3(out_23));
  ADD3 add3_34 (
    .A1(add3_30_s0), .A2(add3_30_s1), .A3(add3_30_s2), .A0(add3_29_s3), .S0(out_24), .S1(P11_2), .S2(out_26),
    .S3(out_27));
  ADD3 add3_35 (
    .A1(add3_26_s3), .A2(add3_22_s3), .A3(1'b0), .A0(add3_30_s3), .S0(P11_3), .S1(out_29), .S2(out_30),
    .S3(P11_4));

  assign P0 = B0;

  // Notes on the sheet:
  //   0
  //   0
  //   0
  //   0
  //   0
  //   0
  //   0
  //   0
  //   0
  //   0
  //   0
  //   B8TOBCD
  //   Converts 8-bit unsigned binary to BCD
endmodule

module B8TCTOBCD (
  input  B0,
  input  B1,
  input  B2,
  input  B3,
  input  B4,
  input  B5,
  input  B6,
  input  B7,
  input  B8,
  input  B9,
  output P0,
  output P1,
  output P2,
  output P3,
  output P4,
  output P5,
  output P6,
  output P7,
  output P8,
  output P9,
  output P10,
  output P11
);

  wire [9:0] adder_1_out, multiplexer_1_out, not_1_out;

  assign not_1_out = ~{B9, B8, B7, B6, B5, B4, B3, B2, B1, B0};  // NOT_Gate not_1, 10 bits wide
  Adder #(.width(10)) adder_1 (.a(not_1_out), .b(10'h1), .out(adder_1_out));  // open: cin, cout
  Multiplexer #(.width(10)) multiplexer_1 (
    .in0({B9, B8, B7, B6, B5, B4, B3, B2, B1, B0}), .in1(adder_1_out), .out(multiplexer_1_out), .sel(B9));
  B8TOBCD b8tobcd_1 (
    .B0(multiplexer_1_out[0]), .B1(multiplexer_1_out[1]), .B2(multiplexer_1_out[2]),
    .B3(multiplexer_1_out[3]), .B4(multiplexer_1_out[4]), .B5(multiplexer_1_out[5]),
    .B6(multiplexer_1_out[6]), .B7(multiplexer_1_out[7]), .B8(multiplexer_1_out[8]),
    .B9(multiplexer_1_out[9]), .P0(P0), .P1(P1), .P2(P2), .P3(P3), .P4(P4), .P5(P5), .P6(P6), .P7(P7),
    .P8(P8), .P9(P9), .P10(P10), .P11(P11));  // open: out_23, out_24, P11_2, out_26, out_27, P11_3, out_29, out_30, P11_4

  // Notes on the sheet:
  //   B8TCTOBCD
  //   Converts 8-bit 2's com to BCD
endmodule

module CALCULATOR (
  output [9:0] out_1
);

  wire add, and_1_out, and_2_out, and_3_out, and_4_out, b8tctobcd_1_p0, b8tctobcd_1_p1, b8tctobcd_1_p2,
       b8tctobcd_1_p3, b8tctobcd_1_p4, b8tctobcd_1_p5, b8tctobcd_1_p6, b8tctobcd_1_p7, b8tctobcd_1_p8,
       b8tctobcd_1_p9, b8tctobcd_1_p10, b8tctobcd_1_p11, back, c, ce, clock_1_out, controlled_buffer_1_out,
       controlled_buffer_23_out, controlled_buffer_26_out, controlled_buffer_31_out,
       controlled_buffer_33_out, controlled_buffer_35_out, d_ff_1_q, d_ff_1_qn, d_ff_2_q, div,
       ic7448_1_out_8, ic7448_1_out_9, ic7448_1_out_10, ic7448_1_out_11, ic7448_1_out_12, ic7448_1_out_13,
       ic7448_1_out_14, ic7448_2_out_8, ic7448_2_out_9, ic7448_2_out_10, ic7448_2_out_11, ic7448_2_out_12,
       ic7448_2_out_13, ic7448_2_out_14, ic7448_3_out_8, ic7448_3_out_9, ic7448_3_out_10, ic7448_3_out_11,
       ic7448_3_out_12, ic7448_3_out_13, ic7448_3_out_14, mul, not_1_out, not_2_out, or_1_out, or_2_out,
       pull_resistor_3_node, pull_resistor_4_node, result, s_r_ff_1_q, s_r_ff_2_q, s_r_ff_3_q, s_r_ff_4_q,
       sub, x0, x1, x2, x3, x4, x5, x6, x7, x8, x9;
  wire [3:0] bit_extender_5_out, bit_extender_6_out, divsimplified_1_res;
  wire [9:0] addercomponent_1_s, addercomponent_2_s, bit_extender_1_out, bit_extender_2_out,
       bit_extender_3_out, bit_extender_4_out, bit_extender_7_out, bit_extender_8_out, bit_extender_9_out,
       controlled_buffer_11_out, dbus, divider_1_out, multiplexer_1_out, multiplexer_2_out,
       multiplexer_3_out, multiplexer_4_out, r1, subcomponent_1_out_3;
  wire [19:0] multiplie10_1_out_3, multiplie10_2_out_3;

  assign controlled_buffer_1_out = x0 ? x0 : 1'bz;  // Controlled_Buffer controlled_buffer_1
  assign controlled_buffer_1_out = x1 ? x1 : 1'bz;  // Controlled_Buffer controlled_buffer_2
  assign controlled_buffer_1_out = x2 ? x2 : 1'bz;  // Controlled_Buffer controlled_buffer_3
  assign controlled_buffer_1_out = x3 ? x3 : 1'bz;  // Controlled_Buffer controlled_buffer_4
  assign controlled_buffer_1_out = x4 ? x4 : 1'bz;  // Controlled_Buffer controlled_buffer_5
  assign controlled_buffer_1_out = x5 ? x5 : 1'bz;  // Controlled_Buffer controlled_buffer_6
  assign controlled_buffer_1_out = x6 ? x6 : 1'bz;  // Controlled_Buffer controlled_buffer_7
  assign controlled_buffer_1_out = x7 ? x7 : 1'bz;  // Controlled_Buffer controlled_buffer_8
  assign controlled_buffer_1_out = x8 ? x8 : 1'bz;  // Controlled_Buffer controlled_buffer_9
  assign controlled_buffer_1_out = x9 ? x9 : 1'bz;  // Controlled_Buffer controlled_buffer_10
  Pull_Resistor pull_resistor_1 (.node(controlled_buffer_1_out));
  assign controlled_buffer_11_out = x0 ? {10{1'b0}} : 10'bz;  // Controlled_Buffer controlled_buffer_11
  assign controlled_buffer_11_out = x1 ? 10'h1 : 10'bz;  // Controlled_Buffer controlled_buffer_12
  assign controlled_buffer_11_out = x2 ? 10'h2 : 10'bz;  // Controlled_Buffer controlled_buffer_13
  Pull_Resistor pull_resistor_2 (.node(controlled_buffer_11_out));
  assign controlled_buffer_11_out = x3 ? 10'h3 : 10'bz;  // Controlled_Buffer controlled_buffer_14
  assign controlled_buffer_11_out = x4 ? 10'h4 : 10'bz;  // Controlled_Buffer controlled_buffer_15
  assign controlled_buffer_11_out = x5 ? 10'h5 : 10'bz;  // Controlled_Buffer controlled_buffer_16
  assign controlled_buffer_11_out = x6 ? 10'h6 : 10'bz;  // Controlled_Buffer controlled_buffer_17
  assign controlled_buffer_11_out = x7 ? 10'h7 : 10'bz;  // Controlled_Buffer controlled_buffer_18
  assign controlled_buffer_11_out = x8 ? 10'h8 : 10'bz;  // Controlled_Buffer controlled_buffer_19
  Pull_Resistor pull_resistor_3 (.node(pull_resistor_3_node));
  assign controlled_buffer_11_out = x9 ? 10'h9 : 10'bz;  // Controlled_Buffer controlled_buffer_20
  assign pull_resistor_3_node = controlled_buffer_1_out ? controlled_buffer_1_out : 1'bz;  // Controlled_Buffer controlled_buffer_21
  assign pull_resistor_3_node = or_1_out ? or_1_out : 1'bz;  // Controlled_Buffer controlled_buffer_22
  or or_1 (or_1_out, sub, mul, add, div);
  or or_2 (or_2_out, controlled_buffer_1_out, result, back);
  Register #(.width(10)) register_1 (
    .D(multiplexer_1_out), .clk(controlled_buffer_23_out), .Q(out_1), .clr(pull_resistor_4_node));  // open: en
  and and_1 (and_1_out, and_4_out, or_2_out);
  assign controlled_buffer_23_out = and_1_out ? and_1_out : 1'bz;  // Controlled_Buffer controlled_buffer_23
  Pull_Resistor pull_resistor_4 (.node(pull_resistor_4_node));
  assign pull_resistor_3_node = result ? result : 1'bz;  // Controlled_Buffer controlled_buffer_24
  Clock clock_1 (.out(clock_1_out));
  assign pull_resistor_3_node = back ? back : 1'bz;  // Controlled_Buffer controlled_buffer_25
  assign controlled_buffer_26_out = add ? add : 1'bz;  // Controlled_Buffer controlled_buffer_26
  S_R_Flip_Flop s_r_ff_1 (
    .S(div), .R(controlled_buffer_33_out), .clk(clock_1_out), .Q(s_r_ff_1_q));  // open: reset, Qn, preset
  Bit_Extender #(.in_width(10), .out_width(10), .\type ("zero")) bit_extender_1 (.in(out_1), .out(bit_extender_1_out));
  Pull_Resistor pull_resistor_5 (.node(controlled_buffer_23_out));
  assign pull_resistor_4_node = ce ? ce : 1'bz;  // Controlled_Buffer controlled_buffer_27
  D_Flip_Flop d_ff_1 (
    .D(pull_resistor_3_node), .clk(clock_1_out), .Q(d_ff_1_q), .Qn(d_ff_1_qn));  // open: preset, reset
  not not_1 (not_1_out, clock_1_out);
  S_R_Flip_Flop s_r_ff_2 (
    .S(sub), .R(controlled_buffer_26_out), .clk(clock_1_out), .Q(s_r_ff_2_q));  // open: reset, Qn, preset
  S_R_Flip_Flop s_r_ff_3 (
    .S(mul), .R(controlled_buffer_33_out), .clk(clock_1_out), .Q(s_r_ff_3_q));  // open: reset, Qn, preset
  Bit_Extender #(.in_width(10), .out_width(10), .\type ("zero")) bit_extender_2 (.in(10'ha), .out(bit_extender_2_out));
  Adder adder_1 ();  // open: a, b, out, cin, cout
  Divider #(.width(10)) divider_1 (.a(out_1), .b(10'ha), .out(divider_1_out));  // open: upper, rem
  assign pull_resistor_4_node = and_2_out ? and_2_out : 1'bz;  // Controlled_Buffer controlled_buffer_28
  assign pull_resistor_4_node = c ? controlled_buffer_31_out : 1'bz;  // Controlled_Buffer controlled_buffer_29
  D_Flip_Flop d_ff_2 (.D(d_ff_1_qn), .clk(not_1_out), .Q(d_ff_2_q));  // open: Qn, preset, reset
  assign controlled_buffer_26_out = controlled_buffer_33_out ? controlled_buffer_33_out : 1'bz;  // Controlled_Buffer controlled_buffer_30
  Pull_Resistor pull_resistor_6 (.node(controlled_buffer_26_out));
  Bit_Extender #(.in_width(10), .out_width(10)) bit_extender_3 (.in(r1), .out(bit_extender_3_out));
  Bit_Extender #(.in_width(10), .out_width(10)) bit_extender_4 (.in(out_1), .out(bit_extender_4_out));
  Bit_Extender #(.in_width(10), .out_width(4)) bit_extender_5 (.in(r1), .out(bit_extender_5_out));
  Bit_Extender #(.in_width(10), .out_width(4)) bit_extender_6 (.in(out_1), .out(bit_extender_6_out));
  Multiplexer #(.width(10)) multiplexer_1 (.in0(multiplexer_2_out), .in1(dbus), .out(multiplexer_1_out), .sel(result));
  Register #(.width(10)) register_2 (.D(dbus), .clk(and_2_out), .Q(r1), .clr(controlled_buffer_31_out));  // open: en
  assign controlled_buffer_31_out = and_3_out ? and_3_out : 1'bz;  // Controlled_Buffer controlled_buffer_31
  and and_2 (and_2_out, and_4_out, or_1_out);
  and and_3 (and_3_out, controlled_buffer_33_out, and_4_out);
  S_R_Flip_Flop s_r_ff_4 (
    .S(or_1_out), .R(controlled_buffer_33_out), .clk(clock_1_out), .Q(s_r_ff_4_q));  // open: reset, Qn, preset
  Multiplie10 multiplie10_1 (.in_1(bit_extender_1_out), .in_2(bit_extender_2_out), .out_3(multiplie10_1_out_3));
  Multiplexer #(.width(10)) multiplexer_2 (
    .in0(addercomponent_2_s), .in1(divider_1_out), .out(multiplexer_2_out), .sel(back));
  assign controlled_buffer_31_out = c ? c : 1'bz;  // Controlled_Buffer controlled_buffer_32
  and and_4 (and_4_out, d_ff_1_q, d_ff_2_q);
  assign controlled_buffer_33_out = controlled_buffer_31_out ? controlled_buffer_31_out : 1'bz;  // Controlled_Buffer controlled_buffer_33
  assign controlled_buffer_33_out = result ? result : 1'bz;  // Controlled_Buffer controlled_buffer_34
  Bit_Extender #(.in_width(20), .out_width(10)) bit_extender_7 (.in(multiplie10_1_out_3), .out(bit_extender_7_out));
  Pull_Resistor pull_resistor_7 (.node(controlled_buffer_31_out));
  Pull_Resistor pull_resistor_8 (.node(controlled_buffer_33_out));
  assign controlled_buffer_35_out = s_r_ff_4_q ? s_r_ff_2_q : 1'bz;  // Controlled_Buffer controlled_buffer_35
  Bit_Extender #(.in_width(20), .out_width(10)) bit_extender_8 (.in(multiplie10_2_out_3), .out(bit_extender_8_out));
  Multiplie10 multiplie10_2 (.in_1(bit_extender_3_out), .in_2(bit_extender_4_out), .out_3(multiplie10_2_out_3));
  DivSimplified divsimplified_1 (.A(bit_extender_5_out), .B(bit_extender_6_out), .Res(divsimplified_1_res));
  _7_Segment_Display u_7_segment_display_1 (
    .g(controlled_buffer_35_out), .f(not_2_out), .a(not_2_out), .b(not_2_out), .e(not_2_out), .d(not_2_out),
    .c(not_2_out), .dp(not_2_out));
  not not_2 (not_2_out, controlled_buffer_35_out);
  Multiplexer #(.width(10)) multiplexer_3 (
    .in0(addercomponent_1_s), .in1(subcomponent_1_out_3), .out(multiplexer_3_out), .sel(s_r_ff_2_q));
  assign bit_extender_9_out = {{6{divsimplified_1_res[3]}}, divsimplified_1_res};  // Bit_Extender bit_extender_9
  AdderComponent addercomponent_1 (.A(r1), .B(out_1), .S(addercomponent_1_s));  // open: COUT
  Multiplexer #(.width(10)) multiplexer_4 (
    .in0(multiplexer_3_out), .in1(bit_extender_8_out), .out(multiplexer_4_out), .sel(s_r_ff_3_q));
  Multiplexer #(.width(10)) multiplexer_5 (
    .in0(multiplexer_4_out), .in1(bit_extender_9_out), .out(dbus), .sel(s_r_ff_1_q));
  AdderComponent addercomponent_2 (
    .A(controlled_buffer_11_out), .B(bit_extender_7_out), .S(addercomponent_2_s));  // open: COUT
  Button button_1 (.out(x1));
  Button button_2 (.out(x4));
  Button button_3 (.out(x7));
  Button button_4 (.out(x0));
  Button button_5 (.out(x2));
  Button button_6 (.out(x5));
  Button button_7 (.out(x8));
  Button button_8 (.out(add));
  Button button_9 (.out(mul));
  Button button_10 (.out(x3));
  Button button_11 (.out(x6));
  Button button_12 (.out(x9));
  Button button_13 (.out(sub));
  Button button_14 (.out(div));
  Button button_15 (.out(c));
  Button button_16 (.out(ce));
  Button button_17 (.out(back));
  Button button_18 (.out(result));
  SubComponent subcomponent_1 (.A(r1), .B(out_1), .out_3(subcomponent_1_out_3));  // open: out_4
  B8TCTOBCD b8tctobcd_1 (
    .B0(out_1[0]), .B1(out_1[1]), .B2(out_1[2]), .B3(out_1[3]), .B4(out_1[4]), .B5(out_1[5]), .B6(out_1[6]),
    .B7(out_1[7]), .B8(out_1[8]), .B9(out_1[9]), .P0(b8tctobcd_1_p0), .P1(b8tctobcd_1_p1),
    .P2(b8tctobcd_1_p2), .P3(b8tctobcd_1_p3), .P4(b8tctobcd_1_p4), .P5(b8tctobcd_1_p5), .P6(b8tctobcd_1_p6),
    .P7(b8tctobcd_1_p7), .P8(b8tctobcd_1_p8), .P9(b8tctobcd_1_p9), .P10(b8tctobcd_1_p10),
    .P11(b8tctobcd_1_p11));
  _7_Segment_Display u_7_segment_display_2 (.g(out_1[9]));  // open: f, a, b, e, d, c, dp
  IC7448 ic7448_1 (
    .in_1(b8tctobcd_1_p1), .in_2(b8tctobcd_1_p2), .in_3(1'b1), .in_4(1'b1), .in_5(1'b1),
    .in_6(b8tctobcd_1_p3), .in_7(b8tctobcd_1_p0), .out_8(ic7448_1_out_8), .out_9(ic7448_1_out_9),
    .out_10(ic7448_1_out_10), .out_11(ic7448_1_out_11), .out_12(ic7448_1_out_12), .out_13(ic7448_1_out_13),
    .out_14(ic7448_1_out_14));
  IC7448 ic7448_2 (
    .in_1(b8tctobcd_1_p5), .in_2(b8tctobcd_1_p6), .in_3(1'b1), .in_4(1'b1), .in_5(1'b1),
    .in_6(b8tctobcd_1_p7), .in_7(b8tctobcd_1_p4), .out_8(ic7448_2_out_8), .out_9(ic7448_2_out_9),
    .out_10(ic7448_2_out_10), .out_11(ic7448_2_out_11), .out_12(ic7448_2_out_12), .out_13(ic7448_2_out_13),
    .out_14(ic7448_2_out_14));
  IC7448 ic7448_3 (
    .in_1(b8tctobcd_1_p9), .in_2(b8tctobcd_1_p10), .in_3(1'b1), .in_4(1'b1), .in_5(1'b1),
    .in_6(b8tctobcd_1_p11), .in_7(b8tctobcd_1_p8), .out_8(ic7448_3_out_8), .out_9(ic7448_3_out_9),
    .out_10(ic7448_3_out_10), .out_11(ic7448_3_out_11), .out_12(ic7448_3_out_12), .out_13(ic7448_3_out_13),
    .out_14(ic7448_3_out_14));
  _7_Segment_Display u_7_segment_display_3 (
    .g(ic7448_3_out_9), .f(ic7448_3_out_8), .a(ic7448_3_out_10), .b(ic7448_3_out_11), .e(ic7448_3_out_14),
    .d(ic7448_3_out_13), .c(ic7448_3_out_12));  // open: dp
  _7_Segment_Display u_7_segment_display_4 (
    .g(ic7448_2_out_9), .f(ic7448_2_out_8), .a(ic7448_2_out_10), .b(ic7448_2_out_11), .e(ic7448_2_out_14),
    .d(ic7448_2_out_13), .c(ic7448_2_out_12));  // open: dp
  _7_Segment_Display u_7_segment_display_5 (
    .g(ic7448_1_out_9), .f(ic7448_1_out_8), .a(ic7448_1_out_10), .b(ic7448_1_out_11), .e(ic7448_1_out_14),
    .d(ic7448_1_out_13), .c(ic7448_1_out_12));  // open: dp

  // Other names for the same wires on the sheet: r2[9:0] = out_1

  // Notes on the sheet:
  //   P10
endmodule

module IC7448 (
  input  in_1,
  input  in_2,
  input  in_3,
  input  in_4,
  input  in_5,
  input  in_6,
  input  in_7,
  output out_8,
  output out_9,
  output out_10,
  output out_11,
  output out_12,
  output out_13,
  output out_14
);

  wire n7447_1_pin9, n7447_1_pin10, n7447_1_pin11, n7447_1_pin12, n7447_1_pin13, n7447_1_pin14, n7447_1_pin15;

  _7447 u_7447_1 (
    .pin1(in_1), .pin2(in_2), .pin3(in_3), .pin4(in_4), .pin5(in_5), .pin6(in_6), .pin7(in_7),
    .pin15(n7447_1_pin15), .pin14(n7447_1_pin14), .pin13(n7447_1_pin13), .pin12(n7447_1_pin12),
    .pin11(n7447_1_pin11), .pin10(n7447_1_pin10), .pin9(n7447_1_pin9));
  not not_1 (out_8, n7447_1_pin15);
  not not_2 (out_9, n7447_1_pin14);
  not not_3 (out_10, n7447_1_pin13);
  not not_4 (out_11, n7447_1_pin12);
  not not_5 (out_12, n7447_1_pin11);
  not not_6 (out_13, n7447_1_pin10);
  not not_7 (out_14, n7447_1_pin9);
endmodule

module Multiplie10 (
  input  [9:0] in_1,
  input  [9:0] in_2,
  output [19:0] out_3
);

  wire adder_2_cout, adder_2_out, adder_3_cout, adder_4_cout, adder_4_out, adder_5_cout, adder_5_out,
       adder_6_cout, adder_7_cout, adder_7_out, adder_8_cout, adder_8_out, adder_9_cout, adder_10_cout,
       adder_10_out, adder_11_cout, adder_11_out, adder_12_cout, adder_12_out, adder_13_cout, adder_13_out,
       adder_14_cout, adder_14_out, adder_15_cout, adder_16_cout, adder_16_out, adder_17_cout, adder_17_out,
       adder_18_cout, adder_19_cout, adder_19_out, adder_20_cout, adder_20_out, adder_21_cout, adder_21_out,
       adder_22_cout, adder_22_out, adder_23_cout, adder_23_out, adder_24_cout, adder_24_out, adder_25_cout,
       adder_25_out, adder_26_cout, adder_26_out, adder_27_cout, adder_27_out, adder_28_cout, adder_29_cout,
       adder_29_out, adder_30_cout, adder_30_out, adder_31_cout, adder_32_cout, adder_32_out, adder_33_cout,
       adder_33_out, adder_34_cout, adder_34_out, adder_35_cout, adder_35_out, adder_36_cout, adder_36_out,
       adder_37_cout, adder_37_out, adder_38_cout, adder_38_out, adder_39_cout, adder_39_out, adder_40_cout,
       adder_40_out, adder_41_cout, adder_41_out, adder_42_cout, adder_42_out, adder_43_cout, adder_43_out,
       adder_44_cout, adder_44_out, adder_45_cout, adder_46_cout, adder_46_out, adder_47_cout, adder_47_out,
       adder_48_cout, adder_49_cout, adder_49_out, adder_50_cout, adder_50_out, adder_51_cout, adder_51_out,
       adder_52_cout, adder_52_out, adder_53_cout, adder_53_out, adder_54_cout, adder_54_out, adder_55_cout,
       adder_55_out, adder_56_cout, adder_56_out, adder_57_cout, adder_57_out, adder_58_cout, adder_58_out,
       adder_59_cout, adder_59_out, adder_60_cout, adder_60_out, adder_61_cout, adder_61_out, adder_62_cout,
       adder_63_cout, adder_64_cout, adder_64_out, adder_65_cout, adder_65_out, adder_66_cout, adder_66_out,
       adder_67_cout, adder_67_out, adder_68_cout, adder_68_out, adder_69_cout, adder_69_out, adder_70_cout,
       adder_70_out, adder_71_cout, adder_71_out, adder_72_cout, adder_72_out, adder_73_cout, adder_73_out,
       adder_74_cout, adder_74_out, adder_75_cout, adder_76_cout, adder_76_out, adder_77_cout, adder_77_out,
       adder_78_cout, adder_78_out, adder_79_cout, adder_79_out, adder_80_cout, adder_81_cout, adder_81_out,
       adder_82_cout, adder_82_out, adder_83_cout, adder_84_cout, adder_84_out, adder_85_cout, adder_85_out,
       adder_86_cout, adder_86_out, adder_87_cout, adder_88_cout, adder_89_cout, adder_89_out, adder_90_cout,
       and_1_out, and_2_out, and_3_out, and_4_out, and_5_out, and_6_out, and_7_out, and_8_out, and_9_out,
       and_10_out, and_11_out, and_12_out, and_13_out, and_14_out, and_15_out, and_16_out, and_17_out,
       and_18_out, and_19_out, and_20_out, and_21_out, and_22_out, and_23_out, and_24_out, and_25_out,
       and_26_out, and_27_out, and_28_out, and_29_out, and_30_out, and_31_out, and_32_out, and_33_out,
       and_34_out, and_35_out, and_36_out, and_37_out, and_38_out, and_39_out, and_40_out, and_41_out,
       and_42_out, and_43_out, and_44_out, and_45_out, and_46_out, and_47_out, and_48_out, and_49_out,
       and_50_out, and_51_out, and_52_out, and_53_out, and_54_out, and_55_out, and_56_out, and_57_out,
       and_58_out, and_59_out, and_60_out, and_61_out, and_62_out, and_63_out, and_64_out, and_65_out,
       and_66_out, and_67_out, and_68_out, and_69_out, and_70_out, and_71_out, and_72_out, and_73_out,
       and_74_out, and_75_out, and_76_out, and_77_out, and_78_out, and_79_out, and_80_out, and_81_out,
       and_82_out, and_83_out, and_84_out, and_85_out, and_86_out, and_87_out, and_88_out, and_89_out,
       and_90_out, and_91_out, and_92_out, and_93_out, and_94_out, and_95_out, and_96_out, and_97_out,
       and_98_out, and_99_out;

  and and_1 (and_1_out, in_2[9], in_1[9]);
  Adder #(.width(1)) adder_1 (.a(and_1_out), .b(adder_2_cout), .out(out_3[18]), .cin(adder_3_cout), .cout(out_3[19]));
  and and_2 (and_2_out, in_2[8], in_1[9]);
  Adder #(.width(1)) adder_2 (
    .a(and_2_out), .b(adder_4_cout), .out(adder_2_out), .cin(adder_5_cout), .cout(adder_2_cout));
  and and_3 (and_3_out, in_2[9], in_1[8]);
  Adder #(.width(1)) adder_3 (.a(and_3_out), .b(adder_2_out), .out(out_3[17]), .cin(adder_6_cout), .cout(adder_3_cout));
  and and_4 (and_4_out, in_2[9], in_1[7]);
  and and_5 (and_5_out, in_2[7], in_1[9]);
  Adder #(.width(1)) adder_4 (
    .a(and_5_out), .b(adder_10_cout), .out(adder_4_out), .cin(adder_7_cout), .cout(adder_4_cout));
  and and_6 (and_6_out, in_2[8], in_1[8]);
  Adder #(.width(1)) adder_5 (
    .a(and_6_out), .b(adder_4_out), .out(adder_5_out), .cin(adder_8_cout), .cout(adder_5_cout));
  Adder #(.width(1)) adder_6 (.a(and_4_out), .b(adder_5_out), .out(out_3[16]), .cin(adder_9_cout), .cout(adder_6_cout));
  and and_7 (and_7_out, in_2[6], in_1[9]);
  and and_8 (and_8_out, in_2[7], in_1[8]);
  Adder #(.width(1)) adder_7 (
    .a(and_8_out), .b(adder_10_out), .out(adder_7_out), .cin(adder_13_cout), .cout(adder_7_cout));
  and and_9 (and_9_out, in_2[8], in_1[7]);
  Adder #(.width(1)) adder_8 (
    .a(and_9_out), .b(adder_7_out), .out(adder_8_out), .cin(adder_14_cout), .cout(adder_8_cout));
  and and_10 (and_10_out, in_2[9], in_1[6]);
  Adder #(.width(1)) adder_9 (
    .a(and_10_out), .b(adder_8_out), .out(out_3[15]), .cin(adder_15_cout), .cout(adder_9_cout));
  Adder #(.width(1)) adder_10 (
    .a(and_7_out), .b(adder_11_cout), .out(adder_10_out), .cin(adder_12_cout), .cout(adder_10_cout));
  and and_11 (and_11_out, in_2[9], in_1[5]);
  and and_12 (and_12_out, in_2[5], in_1[9]);
  Adder #(.width(1)) adder_11 (
    .a(and_12_out), .b(adder_19_cout), .out(adder_11_out), .cin(adder_20_cout), .cout(adder_11_cout));
  and and_13 (and_13_out, in_2[6], in_1[8]);
  Adder #(.width(1)) adder_12 (
    .a(and_13_out), .b(adder_11_out), .out(adder_12_out), .cin(adder_21_cout), .cout(adder_12_cout));
  and and_14 (and_14_out, in_2[7], in_1[7]);
  Adder #(.width(1)) adder_13 (
    .a(and_14_out), .b(adder_12_out), .out(adder_13_out), .cin(adder_16_cout), .cout(adder_13_cout));
  and and_15 (and_15_out, in_2[8], in_1[6]);
  Adder #(.width(1)) adder_14 (
    .a(and_15_out), .b(adder_13_out), .out(adder_14_out), .cin(adder_17_cout), .cout(adder_14_cout));
  Adder #(.width(1)) adder_15 (
    .a(and_11_out), .b(adder_14_out), .out(out_3[14]), .cin(adder_18_cout), .cout(adder_15_cout));
  and and_16 (and_16_out, in_2[5], in_1[8]);
  and and_17 (and_17_out, in_2[6], in_1[7]);
  and and_18 (and_18_out, in_2[7], in_1[6]);
  Adder #(.width(1)) adder_16 (
    .a(and_18_out), .b(adder_21_out), .out(adder_16_out), .cin(adder_26_cout), .cout(adder_16_cout));
  and and_19 (and_19_out, in_2[8], in_1[5]);
  Adder #(.width(1)) adder_17 (
    .a(and_19_out), .b(adder_16_out), .out(adder_17_out), .cin(adder_27_cout), .cout(adder_17_cout));
  and and_20 (and_20_out, in_2[9], in_1[4]);
  Adder #(.width(1)) adder_18 (
    .a(and_20_out), .b(adder_17_out), .out(out_3[13]), .cin(adder_28_cout), .cout(adder_18_cout));
  and and_21 (and_21_out, in_2[4], in_1[9]);
  Adder #(.width(1)) adder_19 (
    .a(and_21_out), .b(adder_22_cout), .out(adder_19_out), .cin(adder_23_cout), .cout(adder_19_cout));
  Adder #(.width(1)) adder_20 (
    .a(and_16_out), .b(adder_19_out), .out(adder_20_out), .cin(adder_24_cout), .cout(adder_20_cout));
  Adder #(.width(1)) adder_21 (
    .a(and_17_out), .b(adder_20_out), .out(adder_21_out), .cin(adder_25_cout), .cout(adder_21_cout));
  and and_22 (and_22_out, in_2[9], in_1[3]);
  and and_23 (and_23_out, in_2[3], in_1[9]);
  Adder #(.width(1)) adder_22 (
    .a(and_23_out), .b(adder_32_cout), .out(adder_22_out), .cin(adder_33_cout), .cout(adder_22_cout));
  and and_24 (and_24_out, in_2[4], in_1[8]);
  Adder #(.width(1)) adder_23 (
    .a(and_24_out), .b(adder_22_out), .out(adder_23_out), .cin(adder_34_cout), .cout(adder_23_cout));
  and and_25 (and_25_out, in_2[5], in_1[7]);
  Adder #(.width(1)) adder_24 (
    .a(and_25_out), .b(adder_23_out), .out(adder_24_out), .cin(adder_35_cout), .cout(adder_24_cout));
  and and_26 (and_26_out, in_2[6], in_1[6]);
  Adder #(.width(1)) adder_25 (
    .a(and_26_out), .b(adder_24_out), .out(adder_25_out), .cin(adder_36_cout), .cout(adder_25_cout));
  and and_27 (and_27_out, in_2[7], in_1[5]);
  Adder #(.width(1)) adder_26 (
    .a(and_27_out), .b(adder_25_out), .out(adder_26_out), .cin(adder_29_cout), .cout(adder_26_cout));
  and and_28 (and_28_out, in_2[8], in_1[4]);
  Adder #(.width(1)) adder_27 (
    .a(and_28_out), .b(adder_26_out), .out(adder_27_out), .cin(adder_30_cout), .cout(adder_27_cout));
  Adder #(.width(1)) adder_28 (
    .a(and_22_out), .b(adder_27_out), .out(out_3[12]), .cin(adder_31_cout), .cout(adder_28_cout));
  and and_29 (and_29_out, in_2[5], in_1[6]);
  and and_30 (and_30_out, in_2[6], in_1[5]);
  and and_31 (and_31_out, in_2[7], in_1[4]);
  Adder #(.width(1)) adder_29 (
    .a(and_31_out), .b(adder_36_out), .out(adder_29_out), .cin(adder_43_cout), .cout(adder_29_cout));
  and and_32 (and_32_out, in_2[8], in_1[3]);
  Adder #(.width(1)) adder_30 (
    .a(and_32_out), .b(adder_29_out), .out(adder_30_out), .cin(adder_44_cout), .cout(adder_30_cout));
  and and_33 (and_33_out, in_2[9], in_1[2]);
  Adder #(.width(1)) adder_31 (
    .a(and_33_out), .b(adder_30_out), .out(out_3[11]), .cin(adder_45_cout), .cout(adder_31_cout));
  and and_34 (and_34_out, in_2[2], in_1[9]);
  Adder #(.width(1)) adder_32 (
    .a(and_34_out), .b(adder_37_cout), .out(adder_32_out), .cin(adder_38_cout), .cout(adder_32_cout));
  and and_35 (and_35_out, in_2[3], in_1[8]);
  Adder #(.width(1)) adder_33 (
    .a(and_35_out), .b(adder_32_out), .out(adder_33_out), .cin(adder_39_cout), .cout(adder_33_cout));
  and and_36 (and_36_out, in_2[4], in_1[7]);
  Adder #(.width(1)) adder_34 (
    .a(and_36_out), .b(adder_33_out), .out(adder_34_out), .cin(adder_40_cout), .cout(adder_34_cout));
  Adder #(.width(1)) adder_35 (
    .a(and_29_out), .b(adder_34_out), .out(adder_35_out), .cin(adder_41_cout), .cout(adder_35_cout));
  Adder #(.width(1)) adder_36 (
    .a(and_30_out), .b(adder_35_out), .out(adder_36_out), .cin(adder_42_cout), .cout(adder_36_cout));
  and and_37 (and_37_out, in_2[9], in_1[1]);
  and and_38 (and_38_out, in_1[9], in_2[1]);
  Adder #(.width(1)) adder_37 (
    .a(adder_49_cout), .b(and_38_out), .out(adder_37_out), .cout(adder_37_cout));  // open: cin
  and and_39 (and_39_out, in_2[2], in_1[8]);
  Adder #(.width(1)) adder_38 (
    .a(and_39_out), .b(adder_37_out), .out(adder_38_out), .cin(adder_50_cout), .cout(adder_38_cout));
  and and_40 (and_40_out, in_2[3], in_1[7]);
  Adder #(.width(1)) adder_39 (
    .a(and_40_out), .b(adder_38_out), .out(adder_39_out), .cin(adder_51_cout), .cout(adder_39_cout));
  and and_41 (and_41_out, in_2[4], in_1[6]);
  Adder #(.width(1)) adder_40 (
    .a(and_41_out), .b(adder_39_out), .out(adder_40_out), .cin(adder_52_cout), .cout(adder_40_cout));
  and and_42 (and_42_out, in_2[5], in_1[5]);
  Adder #(.width(1)) adder_41 (
    .a(and_42_out), .b(adder_40_out), .out(adder_41_out), .cin(adder_53_cout), .cout(adder_41_cout));
  and and_43 (and_43_out, in_2[6], in_1[4]);
  Adder #(.width(1)) adder_42 (
    .a(and_43_out), .b(adder_41_out), .out(adder_42_out), .cin(adder_54_cout), .cout(adder_42_cout));
  and and_44 (and_44_out, in_2[7], in_1[3]);
  Adder #(.width(1)) adder_43 (
    .a(and_44_out), .b(adder_42_out), .out(adder_43_out), .cin(adder_46_cout), .cout(adder_43_cout));
  and and_45 (and_45_out, in_2[8], in_1[2]);
  Adder #(.width(1)) adder_44 (
    .a(and_45_out), .b(adder_43_out), .out(adder_44_out), .cin(adder_47_cout), .cout(adder_44_cout));
  Adder #(.width(1)) adder_45 (
    .a(and_37_out), .b(adder_44_out), .out(out_3[10]), .cin(adder_48_cout), .cout(adder_45_cout));
  and and_46 (and_46_out, in_1[9], in_2[0]);
  and and_47 (and_47_out, in_1[8], in_2[1]);
  and and_48 (and_48_out, in_2[5], in_1[4]);
  and and_49 (and_49_out, in_2[6], in_1[3]);
  and and_50 (and_50_out, in_2[7], in_1[2]);
  Adder #(.width(1)) adder_46 (
    .a(and_50_out), .b(adder_54_out), .out(adder_46_out), .cin(adder_61_cout), .cout(adder_46_cout));
  and and_51 (and_51_out, in_2[8], in_1[1]);
  Adder #(.width(1)) adder_47 (
    .a(and_51_out), .b(adder_46_out), .out(adder_47_out), .cin(adder_62_cout), .cout(adder_47_cout));
  and and_52 (and_52_out, in_2[9], in_1[0]);
  Adder #(.width(1)) adder_48 (.a(and_52_out), .b(adder_47_out), .out(out_3[9]), .cout(adder_48_cout));  // open: cin
  Adder #(.width(1)) adder_49 (
    .a(and_46_out), .b(and_47_out), .out(adder_49_out), .cin(adder_55_cout), .cout(adder_49_cout));
  and and_53 (and_53_out, in_2[2], in_1[7]);
  Adder #(.width(1)) adder_50 (
    .a(and_53_out), .b(adder_49_out), .out(adder_50_out), .cin(adder_56_cout), .cout(adder_50_cout));
  and and_54 (and_54_out, in_2[3], in_1[6]);
  Adder #(.width(1)) adder_51 (
    .a(and_54_out), .b(adder_50_out), .out(adder_51_out), .cin(adder_57_cout), .cout(adder_51_cout));
  and and_55 (and_55_out, in_2[4], in_1[5]);
  Adder #(.width(1)) adder_52 (
    .a(and_55_out), .b(adder_51_out), .out(adder_52_out), .cin(adder_58_cout), .cout(adder_52_cout));
  Adder #(.width(1)) adder_53 (
    .a(and_48_out), .b(adder_52_out), .out(adder_53_out), .cin(adder_59_cout), .cout(adder_53_cout));
  Adder #(.width(1)) adder_54 (
    .a(and_49_out), .b(adder_53_out), .out(adder_54_out), .cin(adder_60_cout), .cout(adder_54_cout));
  and and_56 (and_56_out, in_1[8], in_2[0]);
  and and_57 (and_57_out, in_1[7], in_2[1]);
  Adder #(.width(1)) adder_55 (
    .a(and_56_out), .b(and_57_out), .out(adder_55_out), .cin(adder_64_cout), .cout(adder_55_cout));
  and and_58 (and_58_out, in_2[2], in_1[6]);
  Adder #(.width(1)) adder_56 (
    .a(and_58_out), .b(adder_55_out), .out(adder_56_out), .cin(adder_65_cout), .cout(adder_56_cout));
  and and_59 (and_59_out, in_2[3], in_1[5]);
  Adder #(.width(1)) adder_57 (
    .a(and_59_out), .b(adder_56_out), .out(adder_57_out), .cin(adder_66_cout), .cout(adder_57_cout));
  and and_60 (and_60_out, in_2[4], in_1[4]);
  Adder #(.width(1)) adder_58 (
    .a(and_60_out), .b(adder_57_out), .out(adder_58_out), .cin(adder_67_cout), .cout(adder_58_cout));
  and and_61 (and_61_out, in_2[5], in_1[3]);
  Adder #(.width(1)) adder_59 (
    .a(and_61_out), .b(adder_58_out), .out(adder_59_out), .cin(adder_68_cout), .cout(adder_59_cout));
  and and_62 (and_62_out, in_2[6], in_1[2]);
  Adder #(.width(1)) adder_60 (
    .a(and_62_out), .b(adder_59_out), .out(adder_60_out), .cin(adder_69_cout), .cout(adder_60_cout));
  and and_63 (and_63_out, in_2[7], in_1[1]);
  Adder #(.width(1)) adder_61 (
    .a(and_63_out), .b(adder_60_out), .out(adder_61_out), .cin(adder_63_cout), .cout(adder_61_cout));
  and and_64 (and_64_out, in_2[8], in_1[0]);
  Adder #(.width(1)) adder_62 (.a(and_64_out), .b(adder_61_out), .out(out_3[8]), .cout(adder_62_cout));  // open: cin
  and and_65 (and_65_out, in_1[7], in_2[0]);
  and and_66 (and_66_out, in_1[6], in_2[1]);
  and and_67 (and_67_out, in_2[5], in_1[2]);
  and and_68 (and_68_out, in_2[6], in_1[1]);
  and and_69 (and_69_out, in_2[7], in_1[0]);
  Adder #(.width(1)) adder_63 (.a(and_69_out), .b(adder_69_out), .out(out_3[7]), .cout(adder_63_cout));  // open: cin
  Adder #(.width(1)) adder_64 (
    .a(and_65_out), .b(and_66_out), .out(adder_64_out), .cin(adder_70_cout), .cout(adder_64_cout));
  and and_70 (and_70_out, in_2[2], in_1[5]);
  Adder #(.width(1)) adder_65 (
    .a(and_70_out), .b(adder_64_out), .out(adder_65_out), .cin(adder_71_cout), .cout(adder_65_cout));
  and and_71 (and_71_out, in_2[3], in_1[4]);
  Adder #(.width(1)) adder_66 (
    .a(and_71_out), .b(adder_65_out), .out(adder_66_out), .cin(adder_72_cout), .cout(adder_66_cout));
  and and_72 (and_72_out, in_2[4], in_1[3]);
  Adder #(.width(1)) adder_67 (
    .a(and_72_out), .b(adder_66_out), .out(adder_67_out), .cin(adder_73_cout), .cout(adder_67_cout));
  Adder #(.width(1)) adder_68 (
    .a(and_67_out), .b(adder_67_out), .out(adder_68_out), .cin(adder_74_cout), .cout(adder_68_cout));
  Adder #(.width(1)) adder_69 (
    .a(and_68_out), .b(adder_68_out), .out(adder_69_out), .cin(adder_75_cout), .cout(adder_69_cout));
  and and_73 (and_73_out, in_1[6], in_2[0]);
  and and_74 (and_74_out, in_1[5], in_2[1]);
  Adder #(.width(1)) adder_70 (
    .a(and_73_out), .b(and_74_out), .out(adder_70_out), .cin(adder_76_cout), .cout(adder_70_cout));
  and and_75 (and_75_out, in_2[2], in_1[4]);
  Adder #(.width(1)) adder_71 (
    .a(and_75_out), .b(adder_70_out), .out(adder_71_out), .cin(adder_77_cout), .cout(adder_71_cout));
  and and_76 (and_76_out, in_2[3], in_1[3]);
  Adder #(.width(1)) adder_72 (
    .a(and_76_out), .b(adder_71_out), .out(adder_72_out), .cin(adder_78_cout), .cout(adder_72_cout));
  and and_77 (and_77_out, in_2[4], in_1[2]);
  Adder #(.width(1)) adder_73 (
    .a(and_77_out), .b(adder_72_out), .out(adder_73_out), .cin(adder_79_cout), .cout(adder_73_cout));
  and and_78 (and_78_out, in_2[5], in_1[1]);
  Adder #(.width(1)) adder_74 (
    .a(and_78_out), .b(adder_73_out), .out(adder_74_out), .cin(adder_80_cout), .cout(adder_74_cout));
  and and_79 (and_79_out, in_2[6], in_1[0]);
  Adder #(.width(1)) adder_75 (.a(and_79_out), .b(adder_74_out), .out(out_3[6]), .cout(adder_75_cout));  // open: cin
  and and_80 (and_80_out, in_1[5], in_2[0]);
  and and_81 (and_81_out, in_1[4], in_2[1]);
  and and_82 (and_82_out, in_2[5], in_1[0]);
  Adder #(.width(1)) adder_76 (
    .a(and_80_out), .b(and_81_out), .out(adder_76_out), .cin(adder_84_cout), .cout(adder_76_cout));
  and and_83 (and_83_out, in_2[2], in_1[3]);
  Adder #(.width(1)) adder_77 (
    .a(and_83_out), .b(adder_76_out), .out(adder_77_out), .cin(adder_81_cout), .cout(adder_77_cout));
  and and_84 (and_84_out, in_2[3], in_1[2]);
  Adder #(.width(1)) adder_78 (
    .a(and_84_out), .b(adder_77_out), .out(adder_78_out), .cin(adder_82_cout), .cout(adder_78_cout));
  and and_85 (and_85_out, in_2[4], in_1[1]);
  Adder #(.width(1)) adder_79 (
    .a(and_85_out), .b(adder_78_out), .out(adder_79_out), .cin(adder_83_cout), .cout(adder_79_cout));
  Adder #(.width(1)) adder_80 (.a(and_82_out), .b(adder_79_out), .out(out_3[5]), .cout(adder_80_cout));  // open: cin
  and and_86 (and_86_out, in_1[4], in_2[0]);
  and and_87 (and_87_out, in_1[3], in_2[1]);
  and and_88 (and_88_out, in_2[2], in_1[2]);
  Adder #(.width(1)) adder_81 (
    .a(and_88_out), .b(adder_84_out), .out(adder_81_out), .cin(adder_86_cout), .cout(adder_81_cout));
  and and_89 (and_89_out, in_2[3], in_1[1]);
  Adder #(.width(1)) adder_82 (
    .a(and_89_out), .b(adder_81_out), .out(adder_82_out), .cin(adder_87_cout), .cout(adder_82_cout));
  and and_90 (and_90_out, in_2[4], in_1[0]);
  Adder #(.width(1)) adder_83 (.a(and_90_out), .b(adder_82_out), .out(out_3[4]), .cout(adder_83_cout));  // open: cin
  and and_91 (and_91_out, in_1[3], in_2[0]);
  and and_92 (and_92_out, in_1[2], in_2[1]);
  Adder #(.width(1)) adder_84 (
    .a(and_86_out), .b(and_87_out), .out(adder_84_out), .cin(adder_85_cout), .cout(adder_84_cout));
  Adder #(.width(1)) adder_85 (
    .a(and_91_out), .b(and_92_out), .out(adder_85_out), .cin(adder_89_cout), .cout(adder_85_cout));
  and and_93 (and_93_out, in_2[2], in_1[1]);
  Adder #(.width(1)) adder_86 (
    .a(and_93_out), .b(adder_85_out), .out(adder_86_out), .cin(adder_88_cout), .cout(adder_86_cout));
  and and_94 (and_94_out, in_2[3], in_1[0]);
  Adder #(.width(1)) adder_87 (.a(and_94_out), .b(adder_86_out), .out(out_3[3]), .cout(adder_87_cout));  // open: cin
  and and_95 (and_95_out, in_1[2], in_2[0]);
  and and_96 (and_96_out, in_1[1], in_2[1]);
  and and_97 (and_97_out, in_2[2], in_1[0]);
  Adder #(.width(1)) adder_88 (.a(and_97_out), .b(adder_89_out), .out(out_3[2]), .cout(adder_88_cout));  // open: cin
  and and_98 (and_98_out, in_1[1], in_2[0]);
  and and_99 (and_99_out, in_1[0], in_2[1]);
  Adder #(.width(1)) adder_89 (
    .a(and_95_out), .b(and_96_out), .out(adder_89_out), .cin(adder_90_cout), .cout(adder_89_cout));
  Adder #(.width(1)) adder_90 (.a(and_98_out), .b(and_99_out), .out(out_3[1]), .cout(adder_90_cout));  // open: cin
  and and_100 (out_3[0], in_1[0], in_2[0]);

  // Other names for the same wires on the sheet: XD = in_1[0]; XC = in_1[1]; XB = in_1[2]; XA = in_1[3]; X0 = in_1[4];
  //   X1 = in_1[5]; X2 = in_1[6]; X3 = in_1[7]; X4 = in_1[8]; X5 = in_1[9]; YD = in_2[0]; YC = in_2[1]; YB = in_2[2];
  //   YA = in_2[3]; Y0 = in_2[4]; Y1 = in_2[5]; Y2 = in_2[6]; Y3 = in_2[7]; Y4 = in_2[8]; Y5 = in_2[9]
endmodule

module Multiplie (
  input  [4:0] in_1,
  input  [3:0] in_2,
  output [7:0] out_3
);

  wire adder_1_cout, adder_2_cout, adder_2_out, adder_3_cout, adder_4_cout, adder_4_out, adder_5_cout,
       adder_5_out, adder_6_cout, adder_7_cout, adder_7_out, adder_8_cout, adder_8_out, adder_9_cout,
       adder_10_cout, adder_10_out, adder_11_cout, adder_11_out, adder_12_cout, adder_13_cout, adder_13_out,
       adder_14_cout, adder_15_cout, and_1_out, and_2_out, and_3_out, and_4_out, and_5_out, and_6_out,
       and_7_out, and_8_out, and_9_out, and_10_out, and_11_out, and_12_out, and_13_out, and_14_out,
       and_15_out, and_16_out, and_17_out, and_18_out, and_19_out;

  and and_1 (and_1_out, in_2[3], in_1[4]);
  Adder #(.width(1)) adder_1 (.a(and_1_out), .b(adder_2_cout), .out(out_3[7]), .cin(adder_3_cout), .cout(adder_1_cout));
  and and_2 (and_2_out, in_2[2], in_1[4]);
  Adder #(.width(1)) adder_2 (
    .a(and_2_out), .b(adder_4_cout), .out(adder_2_out), .cin(adder_5_cout), .cout(adder_2_cout));
  and and_3 (and_3_out, in_2[3], in_1[3]);
  Adder #(.width(1)) adder_3 (.a(and_3_out), .b(adder_2_out), .out(out_3[6]), .cin(adder_6_cout), .cout(adder_3_cout));
  and and_4 (and_4_out, in_1[4], in_2[1]);
  Adder #(.width(1)) adder_4 (.a(adder_7_cout), .b(and_4_out), .out(adder_4_out), .cout(adder_4_cout));  // open: cin
  and and_5 (and_5_out, in_2[2], in_1[3]);
  Adder #(.width(1)) adder_5 (
    .a(and_5_out), .b(adder_4_out), .out(adder_5_out), .cin(adder_8_cout), .cout(adder_5_cout));
  and and_6 (and_6_out, in_2[3], in_1[2]);
  Adder #(.width(1)) adder_6 (.a(and_6_out), .b(adder_5_out), .out(out_3[5]), .cin(adder_9_cout), .cout(adder_6_cout));
  and and_7 (and_7_out, in_1[4], in_2[0]);
  and and_8 (and_8_out, in_1[3], in_2[1]);
  Adder #(.width(1)) adder_7 (
    .a(and_7_out), .b(and_8_out), .out(adder_7_out), .cin(adder_10_cout), .cout(adder_7_cout));
  and and_9 (and_9_out, in_2[2], in_1[2]);
  Adder #(.width(1)) adder_8 (
    .a(and_9_out), .b(adder_7_out), .out(adder_8_out), .cin(adder_11_cout), .cout(adder_8_cout));
  and and_10 (and_10_out, in_2[3], in_1[1]);
  Adder #(.width(1)) adder_9 (
    .a(and_10_out), .b(adder_8_out), .out(out_3[4]), .cin(adder_12_cout), .cout(adder_9_cout));
  and and_11 (and_11_out, in_1[3], in_2[0]);
  and and_12 (and_12_out, in_1[2], in_2[1]);
  Adder #(.width(1)) adder_10 (
    .a(and_11_out), .b(and_12_out), .out(adder_10_out), .cin(adder_13_cout), .cout(adder_10_cout));
  and and_13 (and_13_out, in_2[2], in_1[1]);
  Adder #(.width(1)) adder_11 (
    .a(and_13_out), .b(adder_10_out), .out(adder_11_out), .cin(adder_14_cout), .cout(adder_11_cout));
  and and_14 (and_14_out, in_2[3], in_1[0]);
  Adder #(.width(1)) adder_12 (.a(and_14_out), .b(adder_11_out), .out(out_3[3]), .cout(adder_12_cout));  // open: cin
  and and_15 (and_15_out, in_1[2], in_2[0]);
  and and_16 (and_16_out, in_1[1], in_2[1]);
  Adder #(.width(1)) adder_13 (
    .a(and_15_out), .b(and_16_out), .out(adder_13_out), .cin(adder_15_cout), .cout(adder_13_cout));
  and and_17 (and_17_out, in_2[2], in_1[0]);
  Adder #(.width(1)) adder_14 (.a(and_17_out), .b(adder_13_out), .out(out_3[2]), .cout(adder_14_cout));  // open: cin
  and and_18 (and_18_out, in_1[1], in_2[0]);
  and and_19 (and_19_out, in_1[0], in_2[1]);
  Adder #(.width(1)) adder_15 (.a(and_18_out), .b(and_19_out), .out(out_3[1]), .cout(adder_15_cout));  // open: cin
  and and_20 (out_3[0], in_1[0], in_2[0]);

  // Other names for the same wires on the sheet: X0 = in_1[0]; X1 = in_1[1]; X2 = in_1[2]; X3 = in_1[3]; X4 = in_1[4];
  //   Y0 = in_2[0]; Y1 = in_2[1]; Y2 = in_2[2]; Y3 = in_2[3]
endmodule

module Adder8bit (
  input  in_1,
  input  in_2,
  input  in_3,
  input  in_4,
  input  in_5,
  input  in_6,
  input  in_7,
  input  in_8,
  input  in_9,
  input  in_10,
  input  in_11,
  input  in_12,
  input  in_13,
  input  in_14,
  input  in_15,
  input  in_16,
  input  in_17,
  input  in_18,
  input  in_19,
  input  in_20,
  input  Cin,
  output S0,
  output S1,
  output S2,
  output S3,
  output S4,
  output S5,
  output S6,
  output S8,
  output S7,
  output S9,
  output Cout
);

  wire FA0_cout, FA1_cout, FA2_cout, FA3_cout, FA4_cout, FA5_cout, FA6_cout, FA8_cout, fulladder_1_cout;

  FullAdder FA0 (.A(in_1), .B(in_11), .Cin(Cin), .Sum(S0), .Cout(FA0_cout));
  FullAdder FA1 (.A(in_2), .B(in_12), .Cin(FA0_cout), .Sum(S1), .Cout(FA1_cout));
  FullAdder FA2 (.A(in_3), .B(in_13), .Cin(FA1_cout), .Sum(S2), .Cout(FA2_cout));
  FullAdder FA3 (.A(in_4), .B(in_14), .Cin(FA2_cout), .Sum(S3), .Cout(FA3_cout));
  FullAdder FA4 (.A(in_5), .B(in_15), .Cin(FA3_cout), .Sum(S4), .Cout(FA4_cout));
  FullAdder FA5 (.A(in_6), .B(in_16), .Cin(FA4_cout), .Sum(S5), .Cout(FA5_cout));
  FullAdder FA6 (.A(in_7), .B(in_17), .Cin(FA5_cout), .Sum(S6), .Cout(FA6_cout));
  FullAdder FA8 (.A(in_8), .B(in_18), .Cin(FA6_cout), .Sum(S8), .Cout(FA8_cout));
  FullAdder fulladder_1 (.A(in_9), .B(in_19), .Cin(FA8_cout), .Sum(S7), .Cout(fulladder_1_cout));
  FullAdder FA9 (.A(in_10), .B(in_20), .Cin(fulladder_1_cout), .Sum(S9), .Cout(Cout));
endmodule

module FullAdder (
  input  A,
  input  B,
  input  Cin,
  output Sum,
  output Cout
);

  wire and_1_out, and_2_out, xor_1_out;

  xor xor_1 (xor_1_out, A, B);
  xor xor_2 (Sum, xor_1_out, Cin);
  and and_1 (and_1_out, xor_1_out, Cin);
  and and_2 (and_2_out, A, B);
  or or_1 (Cout, and_1_out, and_2_out);
endmodule

module AdderComponent (
  input  [9:0] A,
  input  [9:0] B,
  output [9:0] S,
  output COUT
);

  wire [9:0] adder8bit_1_s0, bit_extender_1_out, bit_extender_2_out;

  Bit_Extender #(.in_width(10), .out_width(10)) bit_extender_1 (.in(A), .out(bit_extender_1_out));
  Bit_Extender #(.in_width(10), .out_width(10)) bit_extender_2 (.in(B), .out(bit_extender_2_out));
  Adder8bit adder8bit_1 (
    .in_1(bit_extender_1_out[0]), .in_2(bit_extender_1_out[1]), .in_3(bit_extender_1_out[2]),
    .in_4(bit_extender_1_out[3]), .in_5(bit_extender_1_out[4]), .in_6(bit_extender_1_out[5]),
    .in_7(bit_extender_1_out[6]), .in_8(bit_extender_1_out[7]), .in_9(bit_extender_1_out[8]),
    .in_10(bit_extender_1_out[9]), .in_11(bit_extender_2_out[0]), .in_12(bit_extender_2_out[1]),
    .in_13(bit_extender_2_out[2]), .in_14(bit_extender_2_out[3]), .in_15(bit_extender_2_out[4]),
    .in_16(bit_extender_2_out[5]), .in_17(bit_extender_2_out[6]), .in_18(bit_extender_2_out[7]),
    .in_19(bit_extender_2_out[8]), .in_20(bit_extender_2_out[9]), .Cin(1'b0), .S0(adder8bit_1_s0[0]),
    .S1(adder8bit_1_s0[1]), .S2(adder8bit_1_s0[2]), .S3(adder8bit_1_s0[3]), .S4(adder8bit_1_s0[4]),
    .S5(adder8bit_1_s0[5]), .S6(adder8bit_1_s0[6]), .S8(adder8bit_1_s0[7]), .S7(adder8bit_1_s0[8]),
    .S9(adder8bit_1_s0[9]), .Cout(COUT));
  Bit_Extender #(.in_width(10), .out_width(10)) bit_extender_3 (.in(adder8bit_1_s0), .out(S));
endmodule

module SubComponent (
  input  [9:0] A,
  input  [9:0] B,
  output [9:0] out_3,
  output out_4
);

  wire not_1_out, not_2_out, not_3_out, not_4_out, not_5_out, not_6_out, not_7_out, not_8_out, not_9_out,
       not_10_out;

  not not_1 (not_1_out, B[0]);
  not not_2 (not_2_out, B[1]);
  not not_3 (not_3_out, B[2]);
  not not_4 (not_4_out, B[3]);
  not not_5 (not_5_out, B[4]);
  not not_6 (not_6_out, B[5]);
  not not_7 (not_7_out, B[6]);
  not not_8 (not_8_out, B[7]);
  not not_9 (not_9_out, B[8]);
  not not_10 (not_10_out, B[9]);
  Adder8bit adder8bit_1 (
    .in_1(A[0]), .in_2(A[1]), .in_3(A[2]), .in_4(A[3]), .in_5(A[4]), .in_6(A[5]), .in_7(A[6]), .in_8(A[7]),
    .in_9(A[8]), .in_10(A[9]), .in_11(not_1_out), .in_12(not_2_out), .in_13(not_3_out), .in_14(not_4_out),
    .in_15(not_5_out), .in_16(not_6_out), .in_17(not_7_out), .in_18(not_8_out), .in_19(not_9_out),
    .in_20(not_10_out), .Cin(1'b1), .S0(out_3[0]), .S1(out_3[1]), .S2(out_3[2]), .S3(out_3[3]),
    .S4(out_3[4]), .S5(out_3[5]), .S6(out_3[6]), .S8(out_3[7]), .S7(out_3[8]), .S9(out_3[9]), .Cout(out_4));
endmodule

module L_1insum (
  input  in_1,
  input  in_2,
  input  cin,
  output \output ,
  output cout
);

  wire and_1_out, and_2_out, xor_1_out;

  xor xor_1 (xor_1_out, in_1, in_2);
  and and_1 (and_1_out, in_1, in_2);
  and and_2 (and_2_out, xor_1_out, cin);
  xor xor_2 (\output , xor_1_out, cin);
  or or_1 (cout, and_2_out, and_1_out);
endmodule

module L_1bitsum (
  input  a0,
  input  a1,
  input  a2,
  input  sign_in_7796079c,
  input  a3,
  output b0,
  output b1,
  output b2,
  output b3,
  output sign_bit_684bf57d
);

  wire l_1insum_2_cout, l_1insum_3_cout, l_1insum_4_cout, l_1insum_5_cout, not_1_out, not_2_out, not_3_out,
       not_4_out, not_5_out;

  L_1insum l_1insum_1 (.in_2(not_1_out), .cin(l_1insum_2_cout), .\output (sign_bit_684bf57d));  // open: in_1, cout
  not not_1 (not_1_out, sign_in_7796079c);
  L_1insum l_1insum_2 (.in_2(not_2_out), .cin(l_1insum_3_cout), .\output (b3), .cout(l_1insum_2_cout));  // open: in_1
  not not_2 (not_2_out, a3);
  L_1insum l_1insum_3 (.in_2(not_3_out), .cin(l_1insum_4_cout), .\output (b2), .cout(l_1insum_3_cout));  // open: in_1
  not not_3 (not_3_out, a2);
  L_1insum l_1insum_4 (.in_2(not_4_out), .cin(l_1insum_5_cout), .\output (b1), .cout(l_1insum_4_cout));  // open: in_1
  not not_4 (not_4_out, a1);
  L_1insum l_1insum_5 (.in_1(1'b1), .in_2(not_5_out), .\output (b0), .cout(l_1insum_5_cout));  // open: cin
  not not_5 (not_5_out, a0);
endmodule

module subt1 (
  input  b3,
  input  b2,
  input  b1,
  input  b0,
  input  a0,
  input  a1,
  input  a2,
  input  a3,
  output c0,
  output c1,
  output c2,
  output c3,
  output isabiggeroreq
);

  wire l_1bitsum_1_b0, l_1bitsum_1_b1, l_1bitsum_1_b2, l_1bitsum_1_b3, l_1bitsum_1_sign_bit_684bf57d,
       l_1insum_1_output, l_1insum_2_cout, l_1insum_2_output, l_1insum_3_cout, l_1insum_3_output,
       l_1insum_4_cout, l_1insum_4_output, l_1insum_5_cout, l_1insum_5_output, not_2_out, not_3_out,
       not_4_out;

  not not_1 (isabiggeroreq, l_1insum_1_output);
  L_1insum l_1insum_1 (
    .in_1(l_1bitsum_1_sign_bit_684bf57d), .in_2(not_2_out), .cin(l_1insum_2_cout),
    .\output (l_1insum_1_output));  // open: cout
  not not_2 (not_2_out, 1'b1);
  not not_3 (not_3_out, isabiggeroreq);
  assign c3 = isabiggeroreq ? l_1insum_2_output : 1'bz;  // Controlled_Buffer controlled_buffer_1
  L_1insum l_1insum_2 (
    .in_1(l_1bitsum_1_b3), .in_2(a3), .cin(l_1insum_3_cout), .\output (l_1insum_2_output),
    .cout(l_1insum_2_cout));
  assign c3 = not_3_out ? a3 : 1'bz;  // Controlled_Buffer controlled_buffer_2
  L_1insum l_1insum_3 (
    .in_1(l_1bitsum_1_b2), .in_2(a2), .cin(l_1insum_4_cout), .\output (l_1insum_3_output),
    .cout(l_1insum_3_cout));
  assign c2 = isabiggeroreq ? l_1insum_3_output : 1'bz;  // Controlled_Buffer controlled_buffer_3
  assign c2 = not_3_out ? a2 : 1'bz;  // Controlled_Buffer controlled_buffer_4
  L_1insum l_1insum_4 (
    .in_1(l_1bitsum_1_b1), .in_2(a1), .cin(l_1insum_5_cout), .\output (l_1insum_4_output),
    .cout(l_1insum_4_cout));
  assign c1 = isabiggeroreq ? l_1insum_4_output : 1'bz;  // Controlled_Buffer controlled_buffer_5
  assign c1 = not_3_out ? a1 : 1'bz;  // Controlled_Buffer controlled_buffer_6
  L_1insum l_1insum_5 (
    .in_1(l_1bitsum_1_b0), .in_2(a0), .cin(1'b0), .\output (l_1insum_5_output), .cout(l_1insum_5_cout));
  assign c0 = isabiggeroreq ? l_1insum_5_output : 1'bz;  // Controlled_Buffer controlled_buffer_7
  assign c0 = not_3_out ? a0 : 1'bz;  // Controlled_Buffer controlled_buffer_8
  not not_4 (not_4_out, 1'b1);
  L_1bitsum l_1bitsum_1 (
    .a0(b0), .a1(b1), .a2(b2), .sign_in_7796079c(not_4_out), .a3(b3), .b0(l_1bitsum_1_b0),
    .b1(l_1bitsum_1_b1), .b2(l_1bitsum_1_b2), .b3(l_1bitsum_1_b3),
    .sign_bit_684bf57d(l_1bitsum_1_sign_bit_684bf57d));
endmodule

module DivComp (
  input  A3,
  input  A2,
  input  A1,
  input  A0,
  input  B3,
  input  B2,
  input  B1,
  input  B0,
  output C3,
  output C2,
  output C1,
  output C0,
  output out_13,
  output out_14,
  output out_15,
  output out_16
);

  wire multiplexer_1_out, multiplexer_2_out, multiplexer_3_out, multiplexer_4_out, multiplexer_5_out,
       multiplexer_6_out, multiplexer_7_out, multiplexer_8_out, multiplexer_9_out, not_1_out, not_2_out,
       not_3_out, subt1_1_c0, subt1_1_c1, subt1_1_c2, subt1_2_c0, subt1_2_c1, subt1_2_c2, subt1_3_c0,
       subt1_3_c1, subt1_3_c2;

  Multiplexer #(.enable("true")) multiplexer_1 (
    .in0(subt1_1_c2), .in1(subt1_1_c2), .out(multiplexer_1_out), .sel(C3), .en(1'b1));
  not not_1 (not_1_out, 1'b1);
  subt1 subt1_1 (
    .b3(B3), .b2(B2), .b1(B1), .b0(B0), .a0(A3), .a1(not_3_out), .a2(not_2_out), .a3(not_1_out),
    .c0(subt1_1_c0), .c1(subt1_1_c1), .c2(subt1_1_c2), .isabiggeroreq(C3));  // open: c3
  Multiplexer #(.enable("true")) multiplexer_2 (
    .in0(subt1_1_c1), .in1(subt1_1_c1), .out(multiplexer_2_out), .sel(C3), .en(1'b1));
  not not_2 (not_2_out, 1'b1);
  not not_3 (not_3_out, 1'b1);
  Multiplexer #(.enable("true")) multiplexer_3 (
    .in0(subt1_1_c0), .in1(subt1_1_c0), .out(multiplexer_3_out), .sel(C3), .en(1'b1));
  subt1 subt1_2 (
    .b3(B3), .b2(B2), .b1(B1), .b0(B0), .a0(A2), .a1(multiplexer_3_out), .a2(multiplexer_2_out),
    .a3(multiplexer_1_out), .c0(subt1_2_c0), .c1(subt1_2_c1), .c2(subt1_2_c2), .isabiggeroreq(C2));  // open: c3
  Multiplexer #(.enable("true")) multiplexer_4 (
    .in0(subt1_2_c2), .in1(subt1_2_c2), .out(multiplexer_4_out), .sel(C2), .en(1'b1));
  Multiplexer #(.enable("true")) multiplexer_5 (
    .in0(subt1_2_c0), .in1(subt1_2_c0), .out(multiplexer_5_out), .sel(C2), .en(1'b1));
  Multiplexer #(.enable("true")) multiplexer_6 (
    .in0(subt1_2_c1), .in1(subt1_2_c1), .out(multiplexer_6_out), .sel(C2), .en(1'b1));
  subt1 subt1_3 (
    .b3(B3), .b2(B2), .b1(B1), .b0(B0), .a0(A1), .a1(multiplexer_5_out), .a2(multiplexer_6_out),
    .a3(multiplexer_4_out), .c0(subt1_3_c0), .c1(subt1_3_c1), .c2(subt1_3_c2), .isabiggeroreq(C1));  // open: c3
  Multiplexer #(.enable("true")) multiplexer_7 (
    .in0(subt1_3_c2), .in1(subt1_3_c2), .out(multiplexer_7_out), .sel(C1), .en(1'b1));
  Multiplexer #(.enable("true")) multiplexer_8 (
    .in0(subt1_3_c0), .in1(subt1_3_c0), .out(multiplexer_8_out), .sel(C1), .en(1'b1));
  Multiplexer #(.enable("true")) multiplexer_9 (
    .in0(subt1_3_c1), .in1(subt1_3_c1), .out(multiplexer_9_out), .sel(C1), .en(1'b1));
  subt1 subt1_4 (
    .b3(B3), .b2(B2), .b1(B1), .b0(B0), .a0(A0), .a1(multiplexer_8_out), .a2(multiplexer_9_out),
    .a3(multiplexer_7_out), .c0(out_16), .c1(out_15), .c2(out_14), .c3(out_13), .isabiggeroreq(C0));
endmodule

module DivSimplified (
  input  [3:0] A,
  input  [3:0] B,
  output [3:0] Res
);

  DivComp divcomp_1 (
    .A3(A[3]), .A2(A[2]), .A1(A[1]), .A0(A[0]), .B3(B[3]), .B2(B[2]), .B1(B[1]), .B0(B[0]), .C3(Res[3]),
    .C2(Res[2]), .C1(Res[1]), .C0(Res[0]));  // open: out_13, out_14, out_15, out_16
endmodule
