// Logisim project Divider1.circ as structural Verilog: 4 circuits, main circuit subt
module subt (
  input  a3,
  input  a2,
  input  a1,
  input  a0,
  input  b3,
  input  b2,
  input  b1,
  input  b0,
  output isabiggeroreq,
  output c3,
  output c2,
  output c1,
  output c0
);

  wire n1bitsum_1_b0, n1bitsum_1_b1, n1bitsum_1_b2, n1bitsum_1_b3, n1bitsum_1_sign_bit, n1in1sum_1_output,
       n1in1sum_2_cout, n1in1sum_2_output, n1in1sum_3_cout, n1in1sum_3_output, n1in1sum_4_cout,
       n1in1sum_4_output, n1in1sum_5_cout, n1in1sum_5_output, not_2_out, not_3_out, not_4_out;

  not not_1 (isabiggeroreq, n1in1sum_1_output);
  not not_2 (not_2_out, 1'b1);
  _1in1sum u_1in1sum_1 (
    ._1input(n1bitsum_1_sign_bit), ._2input(not_2_out), .cin(n1in1sum_2_cout), .\output (n1in1sum_1_output));  // open: cout
  not not_3 (not_3_out, isabiggeroreq);
  assign c3 = isabiggeroreq ? n1in1sum_2_output : 1'bz;  // Controlled_Buffer controlled_buffer_1
  _1in1sum u_1in1sum_2 (
    ._1input(n1bitsum_1_b3), ._2input(a3), .cin(n1in1sum_3_cout), .\output (n1in1sum_2_output),
    .cout(n1in1sum_2_cout));
  assign c3 = not_3_out ? a3 : 1'bz;  // Controlled_Buffer controlled_buffer_2
  assign c2 = isabiggeroreq ? n1in1sum_3_output : 1'bz;  // Controlled_Buffer controlled_buffer_3
  _1in1sum u_1in1sum_3 (
    ._1input(n1bitsum_1_b2), ._2input(a2), .cin(n1in1sum_4_cout), .\output (n1in1sum_3_output),
    .cout(n1in1sum_3_cout));
  assign c2 = not_3_out ? a2 : 1'bz;  // Controlled_Buffer controlled_buffer_4
  assign c1 = isabiggeroreq ? n1in1sum_4_output : 1'bz;  // Controlled_Buffer controlled_buffer_5
  _1in1sum u_1in1sum_4 (
    ._1input(n1bitsum_1_b1), ._2input(a1), .cin(n1in1sum_5_cout), .\output (n1in1sum_4_output),
    .cout(n1in1sum_4_cout));
  assign c1 = not_3_out ? a1 : 1'bz;  // Controlled_Buffer controlled_buffer_6
  assign c0 = isabiggeroreq ? n1in1sum_5_output : 1'bz;  // Controlled_Buffer controlled_buffer_7
  _1in1sum u_1in1sum_5 (
    ._1input(n1bitsum_1_b0), ._2input(a0), .\output (n1in1sum_5_output), .cout(n1in1sum_5_cout));  // open: cin
  assign c0 = not_3_out ? a0 : 1'bz;  // Controlled_Buffer controlled_buffer_8
  not not_4 (not_4_out, 1'b1);
  _1bitsum u_1bitsum_1 (
    .sign_in(not_4_out), .a3(b3), .a2(b2), .a1(b1), .a0(b0), .sign_bit(n1bitsum_1_sign_bit),
    .b3(n1bitsum_1_b3), .b2(n1bitsum_1_b2), .b1(n1bitsum_1_b1), .b0(n1bitsum_1_b0));
endmodule

module _1bitsum (
  input  sign_in,
  input  a3,
  input  a2,
  input  a1,
  input  a0,
  output sign_bit,
  output b3,
  output b2,
  output b1,
  output b0
);

  wire n1in1sum_2_cout, n1in1sum_3_cout, n1in1sum_4_cout, n1in1sum_5_cout, not_1_out, not_2_out, not_3_out,
       not_4_out, not_5_out;

  _1in1sum u_1in1sum_1 (._1input(not_1_out), .cin(n1in1sum_2_cout), .\output (sign_bit));  // open: _2input, cout
  not not_1 (not_1_out, sign_in);
  _1in1sum u_1in1sum_2 (
    ._1input(not_2_out), .cin(n1in1sum_3_cout), .\output (b3), .cout(n1in1sum_2_cout));  // open: _2input
  not not_2 (not_2_out, a3);
  _1in1sum u_1in1sum_3 (
    ._1input(not_4_out), .cin(n1in1sum_4_cout), .\output (b2), .cout(n1in1sum_3_cout));  // open: _2input
  not not_3 (not_3_out, a1);
  not not_4 (not_4_out, a2);
  _1in1sum u_1in1sum_4 (
    ._1input(not_3_out), .cin(n1in1sum_5_cout), .\output (b1), .cout(n1in1sum_4_cout));  // open: _2input
  _1in1sum u_1in1sum_5 (._1input(1'b1), ._2input(not_5_out), .\output (b0), .cout(n1in1sum_5_cout));  // open: cin
  not not_5 (not_5_out, a0);
endmodule

module _1in1sum (
  input  _1input,
  input  _2input,
  input  cin,
  output \output ,
  output cout
);

  wire and_1_out, and_2_out, xor_1_out;

  xor xor_1 (xor_1_out, _1input, _2input);
  and and_1 (and_1_out, _1input, _2input);
  and and_2 (and_2_out, xor_1_out, cin);
  xor xor_2 (\output , xor_1_out, cin);
  or or_1 (cout, and_2_out, and_1_out);
endmodule

module divider_2 (
  input  a3,
  input  a2,
  input  a1,
  input  a0,
  input  b3,
  input  b2,
  input  b1,
  input  b0,
  output c3,
  output c2,
  output c1,
  output c0,
  output d3,
  output d2,
  output d1,
  output d0
);

  wire multiplexer_1_out, multiplexer_2_out, multiplexer_3_out, multiplexer_4_out, multiplexer_5_out,
       multiplexer_6_out, multiplexer_7_out, multiplexer_8_out, multiplexer_9_out, not_1_out, not_2_out,
       not_3_out, subt_1_c0, subt_1_c1, subt_1_c2, subt_2_c0, subt_2_c1, subt_2_c2, subt_3_c0, subt_3_c1,
       subt_3_c2;

  subt subt_1 (
    .a3(not_1_out), .a2(not_2_out), .a1(not_3_out), .a0(a3), .b3(b3), .b2(b2), .b1(b1), .b0(b0),
    .isabiggeroreq(c3), .c2(subt_1_c2), .c1(subt_1_c1), .c0(subt_1_c0));  // open: c3
  Multiplexer multiplexer_1 (.in0(subt_1_c2), .in1(subt_1_c2), .out(multiplexer_1_out), .sel(c3), .en(1'b1));
  not not_1 (not_1_out, 1'b1);
  Multiplexer multiplexer_2 (.in0(subt_1_c1), .in1(subt_1_c1), .out(multiplexer_2_out), .sel(c3), .en(1'b1));
  subt subt_2 (
    .a3(multiplexer_1_out), .a2(multiplexer_2_out), .a1(multiplexer_3_out), .a0(a2), .b3(b3), .b2(b2),
    .b1(b1), .b0(b0), .isabiggeroreq(c2), .c2(subt_2_c2), .c1(subt_2_c1), .c0(subt_2_c0));  // open: c3
  not not_2 (not_2_out, 1'b1);
  not not_3 (not_3_out, 1'b1);
  Multiplexer multiplexer_3 (.in0(subt_1_c0), .in1(subt_1_c0), .out(multiplexer_3_out), .sel(c3), .en(1'b1));
  Multiplexer multiplexer_4 (.in0(subt_2_c2), .in1(subt_2_c2), .out(multiplexer_4_out), .sel(c2), .en(1'b1));
  Multiplexer multiplexer_5 (.in0(subt_2_c0), .in1(subt_2_c0), .out(multiplexer_5_out), .sel(c2), .en(1'b1));
  Multiplexer multiplexer_6 (.in0(subt_2_c1), .in1(subt_2_c1), .out(multiplexer_6_out), .sel(c2), .en(1'b1));
  subt subt_3 (
    .a3(multiplexer_4_out), .a2(multiplexer_6_out), .a1(multiplexer_5_out), .a0(a1), .b3(b3), .b2(b2),
    .b1(b1), .b0(b0), .isabiggeroreq(c1), .c2(subt_3_c2), .c1(subt_3_c1), .c0(subt_3_c0));  // open: c3
  Multiplexer multiplexer_7 (.in0(subt_3_c2), .in1(subt_3_c2), .out(multiplexer_7_out), .sel(c1), .en(1'b1));
  Multiplexer multiplexer_8 (.in0(subt_3_c0), .in1(subt_3_c0), .out(multiplexer_8_out), .sel(c1), .en(1'b1));
  Multiplexer multiplexer_9 (.in0(subt_3_c1), .in1(subt_3_c1), .out(multiplexer_9_out), .sel(c1), .en(1'b1));
  subt subt_4 (
    .a3(multiplexer_7_out), .a2(multiplexer_9_out), .a1(multiplexer_8_out), .a0(a0), .b3(b3), .b2(b2),
    .b1(b1), .b0(b0), .isabiggeroreq(c0), .c3(d3), .c2(d2), .c1(d1), .c0(d0));
endmodule
