// Logisim project Multiplie (2).circ as structural Verilog: 2 circuits, main circuit main
module main (
  input  [4:0] in_1,
  input  [3:0] in_2,
  output [7:0] out_3
);

  wire adder_1_cout, adder_2_cout, adder_2_out, adder_3_cout, adder_4_cout, adder_4_out, adder_5_cout,
       adder_5_out, adder_6_cout, adder_7_cout, adder_7_out, adder_8_cout, adder_8_out, adder_9_cout,
       adder_10_cout, adder_10_out, adder_11_cout, adder_11_out, adder_12_cout, adder_13_cout, adder_13_out,
       adder_14_cout, adder_15_cout, and_1_out, and_2_out, and_3_out, and_4_out, and_5_out, and_6_out,
       and_7_out, and_8_out, and_9_out, and_10_out, and_11_out, and_12_out, and_13_out, and_14_out,
       and_15_out, and_16_out, and_17_out, and_18_out, and_19_out;

  and and_1 (and_1_out, in_2[3], in_1[4]);
  Adder #(.width(1)) adder_1 (.a(and_1_out), .b(adder_2_cout), .out(out_3[7]), .cin(adder_3_cout), .cout(adder_1_cout));
  and and_2 (and_2_out, in_2[2], in_1[4]);
  Adder #(.width(1)) adder_2 (
    .a(and_2_out), .b(adder_4_cout), .out(adder_2_out), .cin(adder_5_cout), .cout(adder_2_cout));
  and and_3 (and_3_out, in_2[3], in_1[3]);
  Adder #(.width(1)) adder_3 (.a(and_3_out), .b(adder_2_out), .out(out_3[6]), .cin(adder_6_cout), .cout(adder_3_cout));
  and and_4 (and_4_out, in_1[4], in_2[1]);
  Adder #(.width(1)) adder_4 (.a(adder_7_cout), .b(and_4_out), .out(adder_4_out), .cout(adder_4_cout));  // open: cin
  and and_5 (and_5_out, in_2[2], in_1[3]);
  Adder #(.width(1)) adder_5 (
    .a(and_5_out), .b(adder_4_out), .out(adder_5_out), .cin(adder_8_cout), .cout(adder_5_cout));
  and and_6 (and_6_out, in_2[3], in_1[2]);
  Adder #(.width(1)) adder_6 (.a(and_6_out), .b(adder_5_out), .out(out_3[5]), .cin(adder_9_cout), .cout(adder_6_cout));
  and and_7 (and_7_out, in_1[4], in_2[0]);
  and and_8 (and_8_out, in_1[3], in_2[1]);
  Adder #(.width(1)) adder_7 (
    .a(and_7_out), .b(and_8_out), .out(adder_7_out), .cin(adder_10_cout), .cout(adder_7_cout));
  and and_9 (and_9_out, in_2[2], in_1[2]);
  Adder #(.width(1)) adder_8 (
    .a(and_9_out), .b(adder_7_out), .out(adder_8_out), .cin(adder_11_cout), .cout(adder_8_cout));
  and and_10 (and_10_out, in_2[3], in_1[1]);
  Adder #(.width(1)) adder_9 (
    .a(and_10_out), .b(adder_8_out), .out(out_3[4]), .cin(adder_12_cout), .cout(adder_9_cout));
  and and_11 (and_11_out, in_1[3], in_2[0]);
  and and_12 (and_12_out, in_1[2], in_2[1]);
  Adder #(.width(1)) adder_10 (
    .a(and_11_out), .b(and_12_out), .out(adder_10_out), .cin(adder_13_cout), .cout(adder_10_cout));
  and and_13 (and_13_out, in_2[2], in_1[1]);
  Adder #(.width(1)) adder_11 (
    .a(and_13_out), .b(adder_10_out), .out(adder_11_out), .cin(adder_14_cout), .cout(adder_11_cout));
  and and_14 (and_14_out, in_2[3], in_1[0]);
  Adder #(.width(1)) adder_12 (.a(and_14_out), .b(adder_11_out), .out(out_3[3]), .cout(adder_12_cout));  // open: cin
  and and_15 (and_15_out, in_1[2], in_2[0]);
  and and_16 (and_16_out, in_1[1], in_2[1]);
  Adder #(.width(1)) adder_13 (
    .a(and_15_out), .b(and_16_out), .out(adder_13_out), .cin(adder_15_cout), .cout(adder_13_cout));
  and and_17 (and_17_out, in_2[2], in_1[0]);
  Adder #(.width(1)) adder_14 (.a(and_17_out), .b(adder_13_out), .out(out_3[2]), .cout(adder_14_cout));  // open: cin
  and and_18 (and_18_out, in_1[1], in_2[0]);
  and and_19 (and_19_out, in_1[0], in_2[1]);
  Adder #(.width(1)) adder_15 (.a(and_18_out), .b(and_19_out), .out(out_3[1]), .cout(adder_15_cout));  // open: cin
  and and_20 (out_3[0], in_1[0], in_2[0]);

  // Other names for the same wires on the sheet: X0 = in_1[0]; X1 = in_1[1]; X2 = in_1[2]; X3 = in_1[3]; X4 = in_1[4];
  //   Y0 = in_2[0]; Y1 = in_2[1]; Y2 = in_2[2]; Y3 = in_2[3]
endmodule

module fsf (
  input  [4:0] in_1,
  input  [3:0] in_2,
  output [7:0] out_3
);

  main main_1 (.in_1(in_1), .in_2(in_2), .out_3(out_3));
endmodule
