// Logisim project Multiplie10 (2).circ as structural Verilog: 1 circuit, main circuit TENxTEN
module TENxTEN (
  input  [9:0] in_1,
  input  [9:0] in_2,
  output [19:0] out_3
);

  wire adder_2_cout, adder_2_out, adder_3_cout, adder_4_cout, adder_4_out, adder_5_cout, adder_5_out,
       adder_6_cout, adder_7_cout, adder_7_out, adder_8_cout, adder_8_out, adder_9_cout, adder_10_cout,
       adder_10_out, adder_11_cout, adder_11_out, adder_12_cout, adder_12_out, adder_13_cout, adder_13_out,
       adder_14_cout, adder_14_out, adder_15_cout, adder_16_cout, adder_16_out, adder_17_cout, adder_17_out,
       adder_18_cout, adder_19_cout, adder_19_out, adder_20_cout, adder_20_out, adder_21_cout, adder_21_out,
       adder_22_cout, adder_22_out, adder_23_cout, adder_23_out, adder_24_cout, adder_24_out, adder_25_cout,
       adder_25_out, adder_26_cout, adder_26_out, adder_27_cout, adder_27_out, adder_28_cout, adder_29_cout,
       adder_29_out, adder_30_cout, adder_30_out, adder_31_cout, adder_32_cout, adder_32_out, adder_33_cout,
       adder_33_out, adder_34_cout, adder_34_out, adder_35_cout, adder_35_out, adder_36_cout, adder_36_out,
       adder_37_cout, adder_37_out, adder_38_cout, adder_38_out, adder_39_cout, adder_39_out, adder_40_cout,
       adder_40_out, adder_41_cout, adder_41_out, adder_42_cout, adder_42_out, adder_43_cout, adder_43_out,
       adder_44_cout, adder_44_out, adder_45_cout, adder_46_cout, adder_46_out, adder_47_cout, adder_47_out,
       adder_48_cout, adder_49_cout, adder_49_out, adder_50_cout, adder_50_out, adder_51_cout, adder_51_out,
       adder_52_cout, adder_52_out, adder_53_cout, adder_53_out, adder_54_cout, adder_54_out, adder_55_cout,
       adder_55_out, adder_56_cout, adder_56_out, adder_57_cout, adder_57_out, adder_58_cout, adder_58_out,
       adder_59_cout, adder_59_out, adder_60_cout, adder_60_out, adder_61_cout, adder_61_out, adder_62_cout,
       adder_63_cout, adder_64_cout, adder_64_out, adder_65_cout, adder_65_out, adder_66_cout, adder_66_out,
       adder_67_cout, adder_67_out, adder_68_cout, adder_68_out, adder_69_cout, adder_69_out, adder_70_cout,
       adder_70_out, adder_71_cout, adder_71_out, adder_72_cout, adder_72_out, adder_73_cout, adder_73_out,
       adder_74_cout, adder_74_out, adder_75_cout, adder_76_cout, adder_76_out, adder_77_cout, adder_77_out,
       adder_78_cout, adder_78_out, adder_79_cout, adder_79_out, adder_80_cout, adder_81_cout, adder_81_out,
       adder_82_cout, adder_82_out, adder_83_cout, adder_84_cout, adder_84_out, adder_85_cout, adder_85_out,
       adder_86_cout, adder_86_out, adder_87_cout, adder_88_cout, adder_89_cout, adder_89_out, adder_90_cout,
       and_1_out, and_2_out, and_3_out, and_4_out, and_5_out, and_6_out, and_7_out, and_8_out, and_9_out,
       and_10_out, and_11_out, and_12_out, and_13_out, and_14_out, and_15_out, and_16_out, and_17_out,
       and_18_out, and_19_out, and_20_out, and_21_out, and_22_out, and_23_out, and_24_out, and_25_out,
       and_26_out, and_27_out, and_28_out, and_29_out, and_30_out, and_31_out, and_32_out, and_33_out,
       and_34_out, and_35_out, and_36_out, and_37_out, and_38_out, and_39_out, and_40_out, and_41_out,
       and_42_out, and_43_out, and_44_out, and_45_out, and_46_out, and_47_out, and_48_out, and_49_out,
       and_50_out, and_51_out, and_52_out, and_53_out, and_54_out, and_55_out, and_56_out, and_57_out,
       and_58_out, and_59_out, and_60_out, and_61_out, and_62_out, and_63_out, and_64_out, and_65_out,
       and_66_out, and_67_out, and_68_out, and_69_out, and_70_out, and_71_out, and_72_out, and_73_out,
       and_74_out, and_75_out, and_76_out, and_77_out, and_78_out, and_79_out, and_80_out, and_81_out,
       and_82_out, and_83_out, and_84_out, and_85_out, and_86_out, and_87_out, and_88_out, and_89_out,
       and_90_out, and_91_out, and_92_out, and_93_out, and_94_out, and_95_out, and_96_out, and_97_out,
       and_98_out, and_99_out;

  and and_1 (and_1_out, in_2[9], in_1[9]);
  Adder #(.width(1)) adder_1 (.a(and_1_out), .b(adder_2_cout), .out(out_3[18]), .cin(adder_3_cout), .cout(out_3[19]));
  and and_2 (and_2_out, in_2[8], in_1[9]);
  Adder #(.width(1)) adder_2 (
    .a(and_2_out), .b(adder_4_cout), .out(adder_2_out), .cin(adder_5_cout), .cout(adder_2_cout));
  and and_3 (and_3_out, in_2[9], in_1[8]);
  Adder #(.width(1)) adder_3 (.a(and_3_out), .b(adder_2_out), .out(out_3[17]), .cin(adder_6_cout), .cout(adder_3_cout));
  and and_4 (and_4_out, in_2[9], in_1[7]);
  and and_5 (and_5_out, in_2[7], in_1[9]);
  Adder #(.width(1)) adder_4 (
    .a(and_5_out), .b(adder_10_cout), .out(adder_4_out), .cin(adder_7_cout), .cout(adder_4_cout));
  and and_6 (and_6_out, in_2[8], in_1[8]);
  Adder #(.width(1)) adder_5 (
    .a(and_6_out), .b(adder_4_out), .out(adder_5_out), .cin(adder_8_cout), .cout(adder_5_cout));
  Adder #(.width(1)) adder_6 (.a(and_4_out), .b(adder_5_out), .out(out_3[16]), .cin(adder_9_cout), .cout(adder_6_cout));
  and and_7 (and_7_out, in_2[6], in_1[9]);
  and and_8 (and_8_out, in_2[7], in_1[8]);
  Adder #(.width(1)) adder_7 (
    .a(and_8_out), .b(adder_10_out), .out(adder_7_out), .cin(adder_13_cout), .cout(adder_7_cout));
  and and_9 (and_9_out, in_2[8], in_1[7]);
  Adder #(.width(1)) adder_8 (
    .a(and_9_out), .b(adder_7_out), .out(adder_8_out), .cin(adder_14_cout), .cout(adder_8_cout));
  and and_10 (and_10_out, in_2[9], in_1[6]);
  Adder #(.width(1)) adder_9 (
    .a(and_10_out), .b(adder_8_out), .out(out_3[15]), .cin(adder_15_cout), .cout(adder_9_cout));
  Adder #(.width(1)) adder_10 (
    .a(and_7_out), .b(adder_11_cout), .out(adder_10_out), .cin(adder_12_cout), .cout(adder_10_cout));
  and and_11 (and_11_out, in_2[9], in_1[5]);
  and and_12 (and_12_out, in_2[5], in_1[9]);
  Adder #(.width(1)) adder_11 (
    .a(and_12_out), .b(adder_19_cout), .out(adder_11_out), .cin(adder_20_cout), .cout(adder_11_cout));
  and and_13 (and_13_out, in_2[6], in_1[8]);
  Adder #(.width(1)) adder_12 (
    .a(and_13_out), .b(adder_11_out), .out(adder_12_out), .cin(adder_21_cout), .cout(adder_12_cout));
  and and_14 (and_14_out, in_2[7], in_1[7]);
  Adder #(.width(1)) adder_13 (
    .a(and_14_out), .b(adder_12_out), .out(adder_13_out), .cin(adder_16_cout), .cout(adder_13_cout));
  and and_15 (and_15_out, in_2[8], in_1[6]);
  Adder #(.width(1)) adder_14 (
    .a(and_15_out), .b(adder_13_out), .out(adder_14_out), .cin(adder_17_cout), .cout(adder_14_cout));
  Adder #(.width(1)) adder_15 (
    .a(and_11_out), .b(adder_14_out), .out(out_3[14]), .cin(adder_18_cout), .cout(adder_15_cout));
  and and_16 (and_16_out, in_2[5], in_1[8]);
  and and_17 (and_17_out, in_2[6], in_1[7]);
  and and_18 (and_18_out, in_2[7], in_1[6]);
  Adder #(.width(1)) adder_16 (
    .a(and_18_out), .b(adder_21_out), .out(adder_16_out), .cin(adder_26_cout), .cout(adder_16_cout));
  and and_19 (and_19_out, in_2[8], in_1[5]);
  Adder #(.width(1)) adder_17 (
    .a(and_19_out), .b(adder_16_out), .out(adder_17_out), .cin(adder_27_cout), .cout(adder_17_cout));
  and and_20 (and_20_out, in_2[9], in_1[4]);
  Adder #(.width(1)) adder_18 (
    .a(and_20_out), .b(adder_17_out), .out(out_3[13]), .cin(adder_28_cout), .cout(adder_18_cout));
  and and_21 (and_21_out, in_2[4], in_1[9]);
  Adder #(.width(1)) adder_19 (
    .a(and_21_out), .b(adder_22_cout), .out(adder_19_out), .cin(adder_23_cout), .cout(adder_19_cout));
  Adder #(.width(1)) adder_20 (
    .a(and_16_out), .b(adder_19_out), .out(adder_20_out), .cin(adder_24_cout), .cout(adder_20_cout));
  Adder #(.width(1)) adder_21 (
    .a(and_17_out), .b(adder_20_out), .out(adder_21_out), .cin(adder_25_cout), .cout(adder_21_cout));
  and and_22 (and_22_out, in_2[9], in_1[3]);
  and and_23 (and_23_out, in_2[3], in_1[9]);
  Adder #(.width(1)) adder_22 (
    .a(and_23_out), .b(adder_32_cout), .out(adder_22_out), .cin(adder_33_cout), .cout(adder_22_cout));
  and and_24 (and_24_out, in_2[4], in_1[8]);
  Adder #(.width(1)) adder_23 (
    .a(and_24_out), .b(adder_22_out), .out(adder_23_out), .cin(adder_34_cout), .cout(adder_23_cout));
  and and_25 (and_25_out, in_2[5], in_1[7]);
  Adder #(.width(1)) adder_24 (
    .a(and_25_out), .b(adder_23_out), .out(adder_24_out), .cin(adder_35_cout), .cout(adder_24_cout));
  and and_26 (and_26_out, in_2[6], in_1[6]);
  Adder #(.width(1)) adder_25 (
    .a(and_26_out), .b(adder_24_out), .out(adder_25_out), .cin(adder_36_cout), .cout(adder_25_cout));
  and and_27 (and_27_out, in_2[7], in_1[5]);
  Adder #(.width(1)) adder_26 (
    .a(and_27_out), .b(adder_25_out), .out(adder_26_out), .cin(adder_29_cout), .cout(adder_26_cout));
  and and_28 (and_28_out, in_2[8], in_1[4]);
  Adder #(.width(1)) adder_27 (
    .a(and_28_out), .b(adder_26_out), .out(adder_27_out), .cin(adder_30_cout), .cout(adder_27_cout));
  Adder #(.width(1)) adder_28 (
    .a(and_22_out), .b(adder_27_out), .out(out_3[12]), .cin(adder_31_cout), .cout(adder_28_cout));
  and and_29 (and_29_out, in_2[5], in_1[6]);
  and and_30 (and_30_out, in_2[6], in_1[5]);
  and and_31 (and_31_out, in_2[7], in_1[4]);
  Adder #(.width(1)) adder_29 (
    .a(and_31_out), .b(adder_36_out), .out(adder_29_out), .cin(adder_43_cout), .cout(adder_29_cout));
  and and_32 (and_32_out, in_2[8], in_1[3]);
  Adder #(.width(1)) adder_30 (
    .a(and_32_out), .b(adder_29_out), .out(adder_30_out), .cin(adder_44_cout), .cout(adder_30_cout));
  and and_33 (and_33_out, in_2[9], in_1[2]);
  Adder #(.width(1)) adder_31 (
    .a(and_33_out), .b(adder_30_out), .out(out_3[11]), .cin(adder_45_cout), .cout(adder_31_cout));
  and and_34 (and_34_out, in_2[2], in_1[9]);
  Adder #(.width(1)) adder_32 (
    .a(and_34_out), .b(adder_37_cout), .out(adder_32_out), .cin(adder_38_cout), .cout(adder_32_cout));
  and and_35 (and_35_out, in_2[3], in_1[8]);
  Adder #(.width(1)) adder_33 (
    .a(and_35_out), .b(adder_32_out), .out(adder_33_out), .cin(adder_39_cout), .cout(adder_33_cout));
  and and_36 (and_36_out, in_2[4], in_1[7]);
  Adder #(.width(1)) adder_34 (
    .a(and_36_out), .b(adder_33_out), .out(adder_34_out), .cin(adder_40_cout), .cout(adder_34_cout));
  Adder #(.width(1)) adder_35 (
    .a(and_29_out), .b(adder_34_out), .out(adder_35_out), .cin(adder_41_cout), .cout(adder_35_cout));
  Adder #(.width(1)) adder_36 (
    .a(and_30_out), .b(adder_35_out), .out(adder_36_out), .cin(adder_42_cout), .cout(adder_36_cout));
  and and_37 (and_37_out, in_2[9], in_1[1]);
  and and_38 (and_38_out, in_1[9], in_2[1]);
  Adder #(.width(1)) adder_37 (
    .a(adder_49_cout), .b(and_38_out), .out(adder_37_out), .cout(adder_37_cout));  // open: cin
  and and_39 (and_39_out, in_2[2], in_1[8]);
  Adder #(.width(1)) adder_38 (
    .a(and_39_out), .b(adder_37_out), .out(adder_38_out), .cin(adder_50_cout), .cout(adder_38_cout));
  and and_40 (and_40_out, in_2[3], in_1[7]);
  Adder #(.width(1)) adder_39 (
    .a(and_40_out), .b(adder_38_out), .out(adder_39_out), .cin(adder_51_cout), .cout(adder_39_cout));
  and and_41 (and_41_out, in_2[4], in_1[6]);
  Adder #(.width(1)) adder_40 (
    .a(and_41_out), .b(adder_39_out), .out(adder_40_out), .cin(adder_52_cout), .cout(adder_40_cout));
  and and_42 (and_42_out, in_2[5], in_1[5]);
  Adder #(.width(1)) adder_41 (
    .a(and_42_out), .b(adder_40_out), .out(adder_41_out), .cin(adder_53_cout), .cout(adder_41_cout));
  and and_43 (and_43_out, in_2[6], in_1[4]);
  Adder #(.width(1)) adder_42 (
    .a(and_43_out), .b(adder_41_out), .out(adder_42_out), .cin(adder_54_cout), .cout(adder_42_cout));
  and and_44 (and_44_out, in_2[7], in_1[3]);
  Adder #(.width(1)) adder_43 (
    .a(and_44_out), .b(adder_42_out), .out(adder_43_out), .cin(adder_46_cout), .cout(adder_43_cout));
  and and_45 (and_45_out, in_2[8], in_1[2]);
  Adder #(.width(1)) adder_44 (
    .a(and_45_out), .b(adder_43_out), .out(adder_44_out), .cin(adder_47_cout), .cout(adder_44_cout));
  Adder #(.width(1)) adder_45 (
    .a(and_37_out), .b(adder_44_out), .out(out_3[10]), .cin(adder_48_cout), .cout(adder_45_cout));
  and and_46 (and_46_out, in_1[9], in_2[0]);
  and and_47 (and_47_out, in_1[8], in_2[1]);
  and and_48 (and_48_out, in_2[5], in_1[4]);
  and and_49 (and_49_out, in_2[6], in_1[3]);
  and and_50 (and_50_out, in_2[7], in_1[2]);
  Adder #(.width(1)) adder_46 (
    .a(and_50_out), .b(adder_54_out), .out(adder_46_out), .cin(adder_61_cout), .cout(adder_46_cout));
  and and_51 (and_51_out, in_2[8], in_1[1]);
  Adder #(.width(1)) adder_47 (
    .a(and_51_out), .b(adder_46_out), .out(adder_47_out), .cin(adder_62_cout), .cout(adder_47_cout));
  and and_52 (and_52_out, in_2[9], in_1[0]);
  Adder #(.width(1)) adder_48 (.a(and_52_out), .b(adder_47_out), .out(out_3[9]), .cout(adder_48_cout));  // open: cin
  Adder #(.width(1)) adder_49 (
    .a(and_46_out), .b(and_47_out), .out(adder_49_out), .cin(adder_55_cout), .cout(adder_49_cout));
  and and_53 (and_53_out, in_2[2], in_1[7]);
  Adder #(.width(1)) adder_50 (
    .a(and_53_out), .b(adder_49_out), .out(adder_50_out), .cin(adder_56_cout), .cout(adder_50_cout));
  and and_54 (and_54_out, in_2[3], in_1[6]);
  Adder #(.width(1)) adder_51 (
    .a(and_54_out), .b(adder_50_out), .out(adder_51_out), .cin(adder_57_cout), .cout(adder_51_cout));
  and and_55 (and_55_out, in_2[4], in_1[5]);
  Adder #(.width(1)) adder_52 (
    .a(and_55_out), .b(adder_51_out), .out(adder_52_out), .cin(adder_58_cout), .cout(adder_52_cout));
  Adder #(.width(1)) adder_53 (
    .a(and_48_out), .b(adder_52_out), .out(adder_53_out), .cin(adder_59_cout), .cout(adder_53_cout));
  Adder #(.width(1)) adder_54 (
    .a(and_49_out), .b(adder_53_out), .out(adder_54_out), .cin(adder_60_cout), .cout(adder_54_cout));
  and and_56 (and_56_out, in_1[8], in_2[0]);
  and and_57 (and_57_out, in_1[7], in_2[1]);
  Adder #(.width(1)) adder_55 (
    .a(and_56_out), .b(and_57_out), .out(adder_55_out), .cin(adder_64_cout), .cout(adder_55_cout));
  and and_58 (and_58_out, in_2[2], in_1[6]);
  Adder #(.width(1)) adder_56 (
    .a(and_58_out), .b(adder_55_out), .out(adder_56_out), .cin(adder_65_cout), .cout(adder_56_cout));
  and and_59 (and_59_out, in_2[3], in_1[5]);
  Adder #(.width(1)) adder_57 (
    .a(and_59_out), .b(adder_56_out), .out(adder_57_out), .cin(adder_66_cout), .cout(adder_57_cout));
  and and_60 (and_60_out, in_2[4], in_1[4]);
  Adder #(.width(1)) adder_58 (
    .a(and_60_out), .b(adder_57_out), .out(adder_58_out), .cin(adder_67_cout), .cout(adder_58_cout));
  and and_61 (and_61_out, in_2[5], in_1[3]);
  Adder #(.width(1)) adder_59 (
    .a(and_61_out), .b(adder_58_out), .out(adder_59_out), .cin(adder_68_cout), .cout(adder_59_cout));
  and and_62 (and_62_out, in_2[6], in_1[2]);
  Adder #(.width(1)) adder_60 (
    .a(and_62_out), .b(adder_59_out), .out(adder_60_out), .cin(adder_69_cout), .cout(adder_60_cout));
  and and_63 (and_63_out, in_2[7], in_1[1]);
  Adder #(.width(1)) adder_61 (
    .a(and_63_out), .b(adder_60_out), .out(adder_61_out), .cin(adder_63_cout), .cout(adder_61_cout));
  and and_64 (and_64_out, in_2[8], in_1[0]);
  Adder #(.width(1)) adder_62 (.a(and_64_out), .b(adder_61_out), .out(out_3[8]), .cout(adder_62_cout));  // open: cin
  and and_65 (and_65_out, in_1[7], in_2[0]);
  and and_66 (and_66_out, in_1[6], in_2[1]);
  and and_67 (and_67_out, in_2[5], in_1[2]);
  and and_68 (and_68_out, in_2[6], in_1[1]);
  and and_69 (and_69_out, in_2[7], in_1[0]);
  Adder #(.width(1)) adder_63 (.a(and_69_out), .b(adder_69_out), .out(out_3[7]), .cout(adder_63_cout));  // open: cin
  Adder #(.width(1)) adder_64 (
    .a(and_65_out), .b(and_66_out), .out(adder_64_out), .cin(adder_70_cout), .cout(adder_64_cout));
  and and_70 (and_70_out, in_2[2], in_1[5]);
  Adder #(.width(1)) adder_65 (
    .a(and_70_out), .b(adder_64_out), .out(adder_65_out), .cin(adder_71_cout), .cout(adder_65_cout));
  and and_71 (and_71_out, in_2[3], in_1[4]);
  Adder #(.width(1)) adder_66 (
    .a(and_71_out), .b(adder_65_out), .out(adder_66_out), .cin(adder_72_cout), .cout(adder_66_cout));
  and and_72 (and_72_out, in_2[4], in_1[3]);
  Adder #(.width(1)) adder_67 (
    .a(and_72_out), .b(adder_66_out), .out(adder_67_out), .cin(adder_73_cout), .cout(adder_67_cout));
  Adder #(.width(1)) adder_68 (
    .a(and_67_out), .b(adder_67_out), .out(adder_68_out), .cin(adder_74_cout), .cout(adder_68_cout));
  Adder #(.width(1)) adder_69 (
    .a(and_68_out), .b(adder_68_out), .out(adder_69_out), .cin(adder_75_cout), .cout(adder_69_cout));
  and and_73 (and_73_out, in_1[6], in_2[0]);
  and and_74 (and_74_out, in_1[5], in_2[1]);
  Adder #(.width(1)) adder_70 (
    .a(and_73_out), .b(and_74_out), .out(adder_70_out), .cin(adder_76_cout), .cout(adder_70_cout));
  and and_75 (and_75_out, in_2[2], in_1[4]);
  Adder #(.width(1)) adder_71 (
    .a(and_75_out), .b(adder_70_out), .out(adder_71_out), .cin(adder_77_cout), .cout(adder_71_cout));
  and and_76 (and_76_out, in_2[3], in_1[3]);
  Adder #(.width(1)) adder_72 (
    .a(and_76_out), .b(adder_71_out), .out(adder_72_out), .cin(adder_78_cout), .cout(adder_72_cout));
  and and_77 (and_77_out, in_2[4], in_1[2]);
  Adder #(.width(1)) adder_73 (
    .a(and_77_out), .b(adder_72_out), .out(adder_73_out), .cin(adder_79_cout), .cout(adder_73_cout));
  and and_78 (and_78_out, in_2[5], in_1[1]);
  Adder #(.width(1)) adder_74 (
    .a(and_78_out), .b(adder_73_out), .out(adder_74_out), .cin(adder_80_cout), .cout(adder_74_cout));
  and and_79 (and_79_out, in_2[6], in_1[0]);
  Adder #(.width(1)) adder_75 (.a(and_79_out), .b(adder_74_out), .out(out_3[6]), .cout(adder_75_cout));  // open: cin
  and and_80 (and_80_out, in_1[5], in_2[0]);
  and and_81 (and_81_out, in_1[4], in_2[1]);
  and and_82 (and_82_out, in_2[5], in_1[0]);
  Adder #(.width(1)) adder_76 (
    .a(and_80_out), .b(and_81_out), .out(adder_76_out), .cin(adder_84_cout), .cout(adder_76_cout));
  and and_83 (and_83_out, in_2[2], in_1[3]);
  Adder #(.width(1)) adder_77 (
    .a(and_83_out), .b(adder_76_out), .out(adder_77_out), .cin(adder_81_cout), .cout(adder_77_cout));
  and and_84 (and_84_out, in_2[3], in_1[2]);
  Adder #(.width(1)) adder_78 (
    .a(and_84_out), .b(adder_77_out), .out(adder_78_out), .cin(adder_82_cout), .cout(adder_78_cout));
  and and_85 (and_85_out, in_2[4], in_1[1]);
  Adder #(.width(1)) adder_79 (
    .a(and_85_out), .b(adder_78_out), .out(adder_79_out), .cin(adder_83_cout), .cout(adder_79_cout));
  Adder #(.width(1)) adder_80 (.a(and_82_out), .b(adder_79_out), .out(out_3[5]), .cout(adder_80_cout));  // open: cin
  and and_86 (and_86_out, in_1[4], in_2[0]);
  and and_87 (and_87_out, in_1[3], in_2[1]);
  and and_88 (and_88_out, in_2[2], in_1[2]);
  Adder #(.width(1)) adder_81 (
    .a(and_88_out), .b(adder_84_out), .out(adder_81_out), .cin(adder_86_cout), .cout(adder_81_cout));
  and and_89 (and_89_out, in_2[3], in_1[1]);
  Adder #(.width(1)) adder_82 (
    .a(and_89_out), .b(adder_81_out), .out(adder_82_out), .cin(adder_87_cout), .cout(adder_82_cout));
  and and_90 (and_90_out, in_2[4], in_1[0]);
  Adder #(.width(1)) adder_83 (.a(and_90_out), .b(adder_82_out), .out(out_3[4]), .cout(adder_83_cout));  // open: cin
  and and_91 (and_91_out, in_1[3], in_2[0]);
  and and_92 (and_92_out, in_1[2], in_2[1]);
  Adder #(.width(1)) adder_84 (
    .a(and_86_out), .b(and_87_out), .out(adder_84_out), .cin(adder_85_cout), .cout(adder_84_cout));
  Adder #(.width(1)) adder_85 (
    .a(and_91_out), .b(and_92_out), .out(adder_85_out), .cin(adder_89_cout), .cout(adder_85_cout));
  and and_93 (and_93_out, in_2[2], in_1[1]);
  Adder #(.width(1)) adder_86 (
    .a(and_93_out), .b(adder_85_out), .out(adder_86_out), .cin(adder_88_cout), .cout(adder_86_cout));
  and and_94 (and_94_out, in_2[3], in_1[0]);
  Adder #(.width(1)) adder_87 (.a(and_94_out), .b(adder_86_out), .out(out_3[3]), .cout(adder_87_cout));  // open: cin
  and and_95 (and_95_out, in_1[2], in_2[0]);
  and and_96 (and_96_out, in_1[1], in_2[1]);
  and and_97 (and_97_out, in_2[2], in_1[0]);
  Adder #(.width(1)) adder_88 (.a(and_97_out), .b(adder_89_out), .out(out_3[2]), .cout(adder_88_cout));  // open: cin
  and and_98 (and_98_out, in_1[1], in_2[0]);
  and and_99 (and_99_out, in_1[0], in_2[1]);
  Adder #(.width(1)) adder_89 (
    .a(and_95_out), .b(and_96_out), .out(adder_89_out), .cin(adder_90_cout), .cout(adder_89_cout));
  Adder #(.width(1)) adder_90 (.a(and_98_out), .b(and_99_out), .out(out_3[1]), .cout(adder_90_cout));  // open: cin
  and and_100 (out_3[0], in_1[0], in_2[0]);

  // Other names for the same wires on the sheet: XD = in_1[0]; XC = in_1[1]; XB = in_1[2]; XA = in_1[3]; X0 = in_1[4];
  //   X1 = in_1[5]; X2 = in_1[6]; X3 = in_1[7]; X4 = in_1[8]; X5 = in_1[9]; YD = in_2[0]; YC = in_2[1]; YB = in_2[2];
  //   YA = in_2[3]; Y0 = in_2[4]; Y1 = in_2[5]; Y2 = in_2[6]; Y3 = in_2[7]; Y4 = in_2[8]; Y5 = in_2[9]
endmodule
